// Digital circuit complex.dig as structural Verilog
module complex (
  input  [15:0] realIN,
  input  [15:0] imageIN,
  output [15:0] realOUT,
  output [15:0] imageOUT,
  output [15:0] grtrFOUR
);

  wire absunit_1_p2, absunit_2_p2, pulldown_1_out;
  wire [15:0] fixedpointmult_1_p3, fixedpointmult_2_p3;

  reals reals_1 (.A(realIN), .B(imageIN), .newREALS(realOUT));
  image image_1 (.a(realIN), .b(imageIN), .newIMAGE(imageOUT));
  // absunit absunit_1: pin names not known; wires that end beside it: realOUT, absunit_1_p2
  // absunit absunit_2: pin names not known; wires that end beside it: imageOUT, absunit_2_p2
  // fixedpointmult fixedpointmult_1: pin names not known; wires that end beside it: absunit_1_p2, absunit_1_p2, fixedpointmult_1_p3
  // fixedpointmult fixedpointmult_2: pin names not known; wires that end beside it: absunit_2_p2, absunit_2_p2, fixedpointmult_2_p3
  Add #(.Bits(16)) add_1 (
    .a(fixedpointmult_1_p3), .b(fixedpointmult_2_p3), .c_i(pulldown_1_out), .s(grtrFOUR));  // open: c_o
  PullDown pulldown_1 (.out(pulldown_1_out));
endmodule
