// Digital circuit image.dig as structural Verilog
module image (
  input  [15:0] a,
  input  [15:0] b,
  output [15:0] newIMAGE
);

  wire pulldown_1_out;
  wire [15:0] add_1_s, arithmetic_shift_out;

  BarrelShifter #(.barrelShifterMode("arithmetic"), .Bits(16)) arithmetic_shift (
    .in(a), .shift(5'b00001), .out(arithmetic_shift_out));
  Add #(.Bits(16)) add_1 (.a(16'h1000), .b(arithmetic_shift_out), .c_i(pulldown_1_out), .s(add_1_s));  // open: c_o
  PullDown pulldown_1 (.out(pulldown_1_out));
  // fixedpointmult fixedpointmult_1: pin names not known; wires that end beside it: add_1_s, b, newIMAGE
endmodule
