// Digital circuit iterationcomplex.dig as structural Verilog
module iterationcomplex (
  input  in_49,
  input  clk,
  input  in_51,
  input  in_52,
  output [15:0] newIMAGE,
  output [15:0] newREALS,
  output [15:0] grtrThanFOUR,
  output [15:0] newIMAGE_2,
  output [15:0] newREALS_2,
  output [15:0] grtrThanFOUR_2,
  output [15:0] newIMAGE_3,
  output [15:0] newREALS_3,
  output [15:0] grtrThanFOUR_3,
  output [15:0] newIMAGE_4,
  output [15:0] newREALS_4,
  output [15:0] grtrThanFOUR_4,
  output [15:0] newIMAGE_5,
  output [15:0] newREALS_5,
  output [15:0] grtrThanFOUR_5,
  output [15:0] newIMAGE_6,
  output [15:0] newREALS_6,
  output [15:0] grtrThanFOUR_6,
  output [15:0] newIMAGE_7,
  output [15:0] newREALS_7,
  output [15:0] grtrThanFOUR_7,
  output [15:0] newIMAGE_8,
  output [15:0] newREALS_8,
  output [15:0] grtrThanFOUR_8,
  output [15:0] newIMAGE_9,
  output [15:0] newREALS_9,
  output [15:0] grtrThanFOUR_9,
  output [15:0] newIMAGE_10,
  output [15:0] newREALS_10,
  output [15:0] grtrThanFOUR_10,
  output [15:0] newIMAGE_11,
  output [15:0] newREALS_11,
  output [15:0] grtrThanFOUR_11,
  output [15:0] newIMAGE_12,
  output [15:0] newREALS_12,
  output [15:0] grtrThanFOUR_12,
  output [15:0] newIMAGE_13,
  output [15:0] newREALS_13,
  output [15:0] grtrThanFOUR_13,
  output [15:0] newIMAGE_14,
  output [15:0] newREALS_14,
  output [15:0] grtrThanFOUR_14,
  output [15:0] newIMAGE_15,
  output [15:0] newREALS_15,
  output [15:0] grtrThanFOUR_15,
  output [15:0] newIMAGE_16,
  output [15:0] newREALS_16,
  output [15:0] grtrThanFOUR_16
);

  wire absunit_2_p2, absunit_3_p2, absunit_4_p2, absunit_5_p2, absunit_6_p2, absunit_8_p2, absunit_9_p2,
       absunit_10_p2, absunit_11_p2, absunit_12_p2, absunit_14_p2, absunit_15_p2, absunit_16_p2,
       absunit_17_p2, absunit_18_p2, absunit_20_p2, absunit_21_p2, absunit_22_p2, absunit_23_p2,
       absunit_24_p2, absunit_26_p2, absunit_27_p2, absunit_28_p2, absunit_29_p2, absunit_30_p2,
       absunit_32_p2, absunit_33_p2, absunit_34_p2, absunit_35_p2, absunit_36_p2, absunit_38_p2,
       absunit_39_p2, absunit_40_p2, absunit_41_p2, absunit_42_p2, absunit_44_p2, absunit_45_p2,
       absunit_46_p2, absunit_47_p2, absunit_48_p2, absunit_50_p2, absunit_51_p2, absunit_52_p2,
       absunit_53_p2, absunit_54_p2, absunit_56_p2, absunit_57_p2, absunit_58_p2, absunit_59_p2,
       absunit_60_p2, absunit_62_p2, absunit_63_p2, absunit_64_p2, absunit_65_p2, absunit_66_p2,
       absunit_68_p2, absunit_69_p2, absunit_70_p2, absunit_71_p2, absunit_72_p2, absunit_74_p2,
       absunit_75_p2, absunit_76_p2, absunit_77_p2, absunit_78_p2, absunit_80_p2, absunit_81_p2,
       absunit_82_p2, absunit_83_p2, absunit_84_p2, absunit_86_p2, absunit_87_p2, absunit_88_p2,
       absunit_89_p2, absunit_90_p2, absunit_92_p2, absunit_93_p2, absunit_94_p2, absunit_95_p2,
       absunit_96_p2, graphiccard_1_d, not_1_out, or_1_out, pulldown_2_out, pulldown_3_out, pulldown_4_out,
       pulldown_5_out, pulldown_6_out, pulldown_7_out, pulldown_8_out, pulldown_9_out, pulldown_10_out,
       pulldown_11_out, pulldown_12_out, pulldown_13_out, pulldown_14_out, pulldown_15_out, pulldown_16_out,
       pulldown_17_out, pulldown_18_out, pulldown_19_out, pulldown_20_out, pulldown_21_out, pulldown_22_out,
       pulldown_23_out, pulldown_24_out, pulldown_25_out, pulldown_26_out, pulldown_27_out, pulldown_28_out,
       pulldown_29_out, pulldown_30_out, pulldown_31_out, pulldown_32_out, pulldown_33_out, pulldown_34_out,
       pulldown_35_out, pulldown_36_out, pulldown_37_out, pulldown_38_out, pulldown_39_out, pulldown_40_out,
       pulldown_41_out, pulldown_42_out, pulldown_43_out, pulldown_44_out, pulldown_45_out, pulldown_46_out,
       pulldown_47_out, pulldown_48_out, pulldown_49_out, pulldown_50_out, pulldown_51_out,
       screenmap128_1_screenclock;
  wire [14:0] pulldown_1_out;
  wire [15:0] absunit_1_p2, absunit_7_p2, absunit_13_p2, absunit_19_p2, absunit_25_p3, absunit_31_p2,
       absunit_37_p2, absunit_43_p2, absunit_49_p2, absunit_55_p2, absunit_61_p2, absunit_67_p2,
       absunit_73_p3, absunit_79_p2, absunit_85_p2, absunit_91_p2, add_1_s, add_4_s, add_7_s, add_10_s,
       add_13_s, add_16_s, add_19_s, add_22_s, add_25_s, add_28_s, add_31_s, add_34_s, add_37_s, add_40_s,
       add_43_s, add_46_s, arithmetic_shift_2_out, arithmetic_shift_3_out, arithmetic_shift_4_out,
       arithmetic_shift_5_out, arithmetic_shift_6_out, arithmetic_shift_7_out, arithmetic_shift_8_out,
       arithmetic_shift_9_out, arithmetic_shift_10_out, arithmetic_shift_11_out, arithmetic_shift_12_out,
       arithmetic_shift_13_out, arithmetic_shift_14_out, arithmetic_shift_15_out, arithmetic_shift_16_out,
       arithmetic_shift_out, fixedpointmult_1_p3, fixedpointmult_2_p2, fixedpointmult_3_p3,
       fixedpointmult_4_p3, fixedpointmult_5_p3, fixedpointmult_6_p3, fixedpointmult_7_p2,
       fixedpointmult_8_p3, fixedpointmult_9_p3, fixedpointmult_10_p3, fixedpointmult_11_p3,
       fixedpointmult_12_p2, fixedpointmult_13_p3, fixedpointmult_14_p3, fixedpointmult_15_p3,
       fixedpointmult_16_p3, fixedpointmult_17_p2, fixedpointmult_18_p3, fixedpointmult_19_p3,
       fixedpointmult_20_p3, fixedpointmult_21_p3, fixedpointmult_22_p2, fixedpointmult_23_p3,
       fixedpointmult_24_p3, fixedpointmult_25_p3, fixedpointmult_26_p3, fixedpointmult_27_p2,
       fixedpointmult_28_p3, fixedpointmult_29_p3, fixedpointmult_30_p3, fixedpointmult_31_p3,
       fixedpointmult_32_p2, fixedpointmult_33_p3, fixedpointmult_34_p3, fixedpointmult_35_p3,
       fixedpointmult_36_p3, fixedpointmult_37_p2, fixedpointmult_38_p3, fixedpointmult_39_p3,
       fixedpointmult_40_p3, fixedpointmult_41_p3, fixedpointmult_42_p2, fixedpointmult_43_p3,
       fixedpointmult_44_p3, fixedpointmult_45_p3, fixedpointmult_46_p3, fixedpointmult_47_p2,
       fixedpointmult_48_p3, fixedpointmult_49_p3, fixedpointmult_50_p3, fixedpointmult_51_p3,
       fixedpointmult_52_p2, fixedpointmult_53_p3, fixedpointmult_54_p3, fixedpointmult_55_p3,
       fixedpointmult_56_p3, fixedpointmult_57_p2, fixedpointmult_58_p3, fixedpointmult_59_p3,
       fixedpointmult_60_p3, fixedpointmult_61_p3, fixedpointmult_62_p2, fixedpointmult_63_p3,
       fixedpointmult_64_p3, fixedpointmult_65_p3, fixedpointmult_66_p3, fixedpointmult_67_p2,
       fixedpointmult_68_p3, fixedpointmult_69_p3, fixedpointmult_70_p3, fixedpointmult_71_p3,
       fixedpointmult_72_p2, fixedpointmult_73_p3, fixedpointmult_74_p3, fixedpointmult_75_p3,
       fixedpointmult_76_p3, fixedpointmult_77_p2, fixedpointmult_78_p3, fixedpointmult_79_p3,
       fixedpointmult_80_p3, multiplexer_2_out, multiplexer_4_out, multiplexer_6_out, multiplexer_8_out,
       multiplexer_10_out, multiplexer_12_out, multiplexer_14_out, multiplexer_16_out, multiplexer_18_out,
       multiplexer_20_out, multiplexer_22_out, multiplexer_24_out, multiplexer_26_out, multiplexer_28_out,
       multiplexer_30_out, multiplexer_32_out, neg_1_out, neg_2_out, neg_3_out, neg_4_out, neg_5_out,
       neg_6_out, neg_7_out, neg_8_out, neg_9_out, neg_10_out, neg_11_out, neg_12_out, neg_13_out,
       neg_14_out, neg_15_out, neg_16_out, neg_17_out, neg_18_out, neg_19_out, neg_20_out, neg_21_out,
       neg_22_out, neg_23_out, neg_24_out, neg_25_out, neg_26_out, neg_27_out, neg_28_out, neg_29_out,
       neg_30_out, neg_31_out, neg_32_out, screenmap128_1_mapimage, screenmap128_1_mapreal, sub_1_s, sub_2_s,
       sub_3_s, sub_4_s, sub_5_s, sub_6_s, sub_7_s, sub_8_s, sub_9_s, sub_10_s, sub_11_s, sub_12_s, sub_13_s,
       sub_14_s, sub_15_s, sub_16_s;

  screenMAP128 screenmap128_1 (
    .ResetToNeg2(in_49), .clock(clk), .mapREAL(screenmap128_1_mapreal), .mapIMAGE(screenmap128_1_mapimage),
    .Xcoord(pulldown_1_out[6:0]), .Ycoord(pulldown_1_out[13:7]), .screenCLOCK(screenmap128_1_screenclock));
  PullDown pulldown_1 (.out(pulldown_1_out[14]));
  GraphicCard #(.graphicHeight(128), .graphicWidth(128)) graphiccard_1 (
    .A(pulldown_1_out), .str(screenmap128_1_screenclock), .C(screenmap128_1_screenclock),
    .ld(pulldown_2_out), .B(pulldown_2_out), .D(graphiccard_1_d));
  PullDown pulldown_2 (.out(pulldown_2_out));
  Multiplexer multiplexer_1 (.sel(in_51), .in_0(not_1_out), .in_1(in_52), .out(graphiccard_1_d));
  not not_1 (not_1_out, or_1_out);
  // absunit absunit_1: pin names not known; wires that end beside it: screenmap128_1_mapreal, absunit_1_p2
  // absunit absunit_2: pin names not known; wires that end beside it: screenmap128_1_mapreal, absunit_2_p2
  // absunit absunit_3: pin names not known; wires that end beside it: screenmap128_1_mapimage, absunit_3_p2
  BarrelShifter #(.barrelShifterMode("arithmetic"), .Bits(16)) arithmetic_shift (
    .in(absunit_1_p2), .shift(5'b00001), .out(arithmetic_shift_out));
  Neg #(.Bits(16)) neg_1 (.in(arithmetic_shift_out), .out(neg_1_out));
  // fixedpointmult fixedpointmult_1: pin names not known; wires that end beside it: absunit_2_p2, screenmap128_1_mapreal, fixedpointmult_1_p3
  // fixedpointmult fixedpointmult_2: pin names not known; wires that end beside it: absunit_3_p2, fixedpointmult_2_p2
  Multiplexer #(.Bits(16)) multiplexer_2 (
    .sel(screenmap128_1_mapreal[15]), .in_0(arithmetic_shift_out), .in_1(neg_1_out), .out(multiplexer_2_out));
  PullDown pulldown_3 (.out(pulldown_3_out));
  // absunit absunit_4: pin names not known; wires that end beside it: screenmap128_1_mapimage, absunit_4_p2
  Sub #(.Bits(16)) sub_1 (
    .a(fixedpointmult_1_p3), .b(fixedpointmult_2_p2), .c_i(pulldown_3_out), .s(sub_1_s));  // open: c_o
  Add #(.Bits(16)) add_1 (.a(16'h1000), .b(multiplexer_2_out), .c_i(pulldown_4_out), .s(add_1_s));  // open: c_o
  PullDown pulldown_4 (.out(pulldown_4_out));
  Add #(.Bits(16)) add_2 (.a(screenmap128_1_mapreal), .b(sub_1_s), .c_i(pulldown_3_out), .s(newREALS));  // open: c_o
  // fixedpointmult fixedpointmult_3: pin names not known; wires that end beside it: add_1_s, absunit_4_p2, fixedpointmult_3_p3
  // absunit absunit_5: pin names not known; wires that end beside it: newREALS, absunit_5_p2
  // absunit absunit_6: pin names not known; wires that end beside it: newIMAGE, absunit_6_p2
  Neg #(.Bits(16)) neg_2 (.in(fixedpointmult_3_p3), .out(neg_2_out));
  // fixedpointmult fixedpointmult_4: pin names not known; wires that end beside it: absunit_5_p2, absunit_5_p2, fixedpointmult_4_p3
  // fixedpointmult fixedpointmult_5: pin names not known; wires that end beside it: absunit_6_p2, absunit_6_p2, fixedpointmult_5_p3, newIMAGE
  Multiplexer #(.Bits(16)) multiplexer_3 (
    .sel(screenmap128_1_mapimage[15]), .in_0(fixedpointmult_3_p3), .in_1(neg_2_out), .out(newIMAGE));
  Add #(.Bits(16)) add_3 (
    .a(fixedpointmult_4_p3), .b(fixedpointmult_5_p3), .c_i(pulldown_5_out), .s(grtrThanFOUR));  // open: c_o
  PullDown pulldown_5 (.out(pulldown_5_out));
  // absunit absunit_7: pin names not known; wires that end beside it: newREALS, absunit_7_p2
  // absunit absunit_8: pin names not known; wires that end beside it: newREALS, absunit_8_p2
  // absunit absunit_9: pin names not known; wires that end beside it: newIMAGE, absunit_9_p2
  BarrelShifter #(.barrelShifterMode("arithmetic"), .Bits(16)) arithmetic_shift_2 (
    .in(absunit_7_p2), .shift(5'b00001), .out(arithmetic_shift_2_out));
  Neg #(.Bits(16)) neg_3 (.in(arithmetic_shift_2_out), .out(neg_3_out));
  // fixedpointmult fixedpointmult_6: pin names not known; wires that end beside it: absunit_8_p2, newREALS, fixedpointmult_6_p3
  // fixedpointmult fixedpointmult_7: pin names not known; wires that end beside it: absunit_9_p2, fixedpointmult_7_p2
  Multiplexer #(.Bits(16)) multiplexer_4 (
    .sel(newREALS[15]), .in_0(arithmetic_shift_2_out), .in_1(neg_3_out), .out(multiplexer_4_out));
  PullDown pulldown_6 (.out(pulldown_6_out));
  // absunit absunit_10: pin names not known; wires that end beside it: newIMAGE, absunit_10_p2
  Sub #(.Bits(16)) sub_2 (
    .a(fixedpointmult_6_p3), .b(fixedpointmult_7_p2), .c_i(pulldown_6_out), .s(sub_2_s));  // open: c_o
  Add #(.Bits(16)) add_4 (.a(16'h1000), .b(multiplexer_4_out), .c_i(pulldown_7_out), .s(add_4_s));  // open: c_o
  PullDown pulldown_7 (.out(pulldown_7_out));
  Add #(.Bits(16)) add_5 (.a(newREALS), .b(sub_2_s), .c_i(pulldown_6_out), .s(newREALS_2));  // open: c_o
  // fixedpointmult fixedpointmult_8: pin names not known; wires that end beside it: add_4_s, absunit_10_p2, fixedpointmult_8_p3
  // absunit absunit_11: pin names not known; wires that end beside it: newREALS_2, absunit_11_p2
  // absunit absunit_12: pin names not known; wires that end beside it: newIMAGE_2, absunit_12_p2
  Neg #(.Bits(16)) neg_4 (.in(fixedpointmult_8_p3), .out(neg_4_out));
  // fixedpointmult fixedpointmult_9: pin names not known; wires that end beside it: absunit_11_p2, absunit_11_p2, fixedpointmult_9_p3
  // fixedpointmult fixedpointmult_10: pin names not known; wires that end beside it: absunit_12_p2, absunit_12_p2, fixedpointmult_10_p3, newIMAGE_2
  Multiplexer #(.Bits(16)) multiplexer_5 (
    .sel(newIMAGE[15]), .in_0(fixedpointmult_8_p3), .in_1(neg_4_out), .out(newIMAGE_2));
  Add #(.Bits(16)) add_6 (
    .a(fixedpointmult_9_p3), .b(fixedpointmult_10_p3), .c_i(pulldown_8_out), .s(grtrThanFOUR_2));  // open: c_o
  PullDown pulldown_8 (.out(pulldown_8_out));
  // absunit absunit_13: pin names not known; wires that end beside it: newREALS_2, absunit_13_p2
  BarrelShifter #(.barrelShifterMode("arithmetic"), .Bits(16)) arithmetic_shift_3 (
    .in(absunit_13_p2), .shift(5'b00001), .out(arithmetic_shift_3_out));
  // absunit absunit_14: pin names not known; wires that end beside it: newREALS_2, absunit_14_p2
  // absunit absunit_15: pin names not known; wires that end beside it: newIMAGE_2, absunit_15_p2
  Neg #(.Bits(16)) neg_5 (.in(arithmetic_shift_3_out), .out(neg_5_out));
  // fixedpointmult fixedpointmult_11: pin names not known; wires that end beside it: absunit_14_p2, newREALS_2, fixedpointmult_11_p3
  // fixedpointmult fixedpointmult_12: pin names not known; wires that end beside it: absunit_15_p2, fixedpointmult_12_p2
  Multiplexer #(.Bits(16)) multiplexer_6 (
    .sel(newREALS_2[15]), .in_0(arithmetic_shift_3_out), .in_1(neg_5_out), .out(multiplexer_6_out));
  // absunit absunit_16: pin names not known; wires that end beside it: newIMAGE_2, absunit_16_p2
  Sub #(.Bits(16)) sub_3 (
    .a(fixedpointmult_11_p3), .b(fixedpointmult_12_p2), .c_i(pulldown_9_out), .s(sub_3_s));  // open: c_o
  PullDown pulldown_9 (.out(pulldown_9_out));
  Add #(.Bits(16)) add_7 (.a(16'h1000), .b(multiplexer_6_out), .c_i(pulldown_10_out), .s(add_7_s));  // open: c_o
  PullDown pulldown_10 (.out(pulldown_10_out));
  Add #(.Bits(16)) add_8 (.a(newREALS_2), .b(sub_3_s), .c_i(pulldown_9_out), .s(newREALS_3));  // open: c_o
  // absunit absunit_17: pin names not known; wires that end beside it: newREALS_3, absunit_17_p2
  // absunit absunit_18: pin names not known; wires that end beside it: newIMAGE_3, absunit_18_p2
  // fixedpointmult fixedpointmult_13: pin names not known; wires that end beside it: add_7_s, absunit_16_p2, fixedpointmult_13_p3
  // fixedpointmult fixedpointmult_14: pin names not known; wires that end beside it: absunit_17_p2, absunit_17_p2, fixedpointmult_14_p3
  // fixedpointmult fixedpointmult_15: pin names not known; wires that end beside it: absunit_18_p2, absunit_18_p2, fixedpointmult_15_p3, newIMAGE_3
  Neg #(.Bits(16)) neg_6 (.in(fixedpointmult_13_p3), .out(neg_6_out));
  Multiplexer #(.Bits(16)) multiplexer_7 (
    .sel(newIMAGE_2[15]), .in_0(fixedpointmult_13_p3), .in_1(neg_6_out), .out(newIMAGE_3));
  PullDown pulldown_11 (.out(pulldown_11_out));
  Add #(.Bits(16)) add_9 (
    .a(fixedpointmult_14_p3), .b(fixedpointmult_15_p3), .c_i(pulldown_11_out), .s(grtrThanFOUR_3));  // open: c_o
  // absunit absunit_19: pin names not known; wires that end beside it: newREALS_3, absunit_19_p2
  BarrelShifter #(.barrelShifterMode("arithmetic"), .Bits(16)) arithmetic_shift_4 (
    .in(absunit_19_p2), .shift(5'b00001), .out(arithmetic_shift_4_out));
  // absunit absunit_20: pin names not known; wires that end beside it: newREALS_3, absunit_20_p2
  // absunit absunit_21: pin names not known; wires that end beside it: newIMAGE_3, absunit_21_p2
  Neg #(.Bits(16)) neg_7 (.in(arithmetic_shift_4_out), .out(neg_7_out));
  // fixedpointmult fixedpointmult_16: pin names not known; wires that end beside it: absunit_20_p2, newREALS_3, fixedpointmult_16_p3
  // fixedpointmult fixedpointmult_17: pin names not known; wires that end beside it: absunit_21_p2, fixedpointmult_17_p2
  Multiplexer #(.Bits(16)) multiplexer_8 (
    .sel(newREALS_3[15]), .in_0(arithmetic_shift_4_out), .in_1(neg_7_out), .out(multiplexer_8_out));
  // absunit absunit_22: pin names not known; wires that end beside it: newIMAGE_3, absunit_22_p2
  Sub #(.Bits(16)) sub_4 (
    .a(fixedpointmult_16_p3), .b(fixedpointmult_17_p2), .c_i(pulldown_12_out), .s(sub_4_s));  // open: c_o
  PullDown pulldown_12 (.out(pulldown_12_out));
  Add #(.Bits(16)) add_10 (.a(16'h1000), .b(multiplexer_8_out), .c_i(pulldown_13_out), .s(add_10_s));  // open: c_o
  PullDown pulldown_13 (.out(pulldown_13_out));
  Add #(.Bits(16)) add_11 (.a(newREALS_3), .b(sub_4_s), .c_i(pulldown_12_out), .s(newREALS_4));  // open: c_o
  // absunit absunit_23: pin names not known; wires that end beside it: newREALS_4, absunit_23_p2
  // absunit absunit_24: pin names not known; wires that end beside it: newIMAGE_4, absunit_24_p2
  // fixedpointmult fixedpointmult_18: pin names not known; wires that end beside it: add_10_s, absunit_22_p2, fixedpointmult_18_p3
  // fixedpointmult fixedpointmult_19: pin names not known; wires that end beside it: absunit_23_p2, absunit_23_p2, fixedpointmult_19_p3
  // fixedpointmult fixedpointmult_20: pin names not known; wires that end beside it: absunit_24_p2, absunit_24_p2, fixedpointmult_20_p3, newIMAGE_4
  Neg #(.Bits(16)) neg_8 (.in(fixedpointmult_18_p3), .out(neg_8_out));
  Multiplexer #(.Bits(16)) multiplexer_9 (
    .sel(newIMAGE_3[15]), .in_0(fixedpointmult_18_p3), .in_1(neg_8_out), .out(newIMAGE_4));
  PullDown pulldown_14 (.out(pulldown_14_out));
  Add #(.Bits(16)) add_12 (
    .a(fixedpointmult_19_p3), .b(fixedpointmult_20_p3), .c_i(pulldown_14_out), .s(grtrThanFOUR_4));  // open: c_o
  // absunit absunit_25: pin names not known; wires that end beside it: newREALS_4, newREALS_4, absunit_25_p3
  // absunit absunit_26: pin names not known; wires that end beside it: newREALS_4, absunit_26_p2
  // absunit absunit_27: pin names not known; wires that end beside it: newIMAGE_4, absunit_27_p2
  BarrelShifter #(.barrelShifterMode("arithmetic"), .Bits(16)) arithmetic_shift_5 (
    .in(absunit_25_p3), .shift(5'b00001), .out(arithmetic_shift_5_out));
  Neg #(.Bits(16)) neg_9 (.in(arithmetic_shift_5_out), .out(neg_9_out));
  // fixedpointmult fixedpointmult_21: pin names not known; wires that end beside it: absunit_26_p2, newREALS_4, fixedpointmult_21_p3
  // fixedpointmult fixedpointmult_22: pin names not known; wires that end beside it: absunit_27_p2, fixedpointmult_22_p2
  Multiplexer #(.Bits(16)) multiplexer_10 (
    .sel(newREALS_4[15]), .in_0(arithmetic_shift_5_out), .in_1(neg_9_out), .out(multiplexer_10_out));
  // absunit absunit_28: pin names not known; wires that end beside it: newIMAGE_4, absunit_28_p2
  Sub #(.Bits(16)) sub_5 (
    .a(fixedpointmult_21_p3), .b(fixedpointmult_22_p2), .c_i(pulldown_15_out), .s(sub_5_s));  // open: c_o
  PullDown pulldown_15 (.out(pulldown_15_out));
  Add #(.Bits(16)) add_13 (.a(16'h1000), .b(multiplexer_10_out), .c_i(pulldown_16_out), .s(add_13_s));  // open: c_o
  PullDown pulldown_16 (.out(pulldown_16_out));
  Add #(.Bits(16)) add_14 (.a(newREALS_4), .b(sub_5_s), .c_i(pulldown_15_out), .s(newREALS_5));  // open: c_o
  // absunit absunit_29: pin names not known; wires that end beside it: newREALS_5, absunit_29_p2
  // absunit absunit_30: pin names not known; wires that end beside it: newIMAGE_5, absunit_30_p2
  // fixedpointmult fixedpointmult_23: pin names not known; wires that end beside it: add_13_s, absunit_28_p2, fixedpointmult_23_p3
  Neg #(.Bits(16)) neg_10 (.in(fixedpointmult_23_p3), .out(neg_10_out));
  // fixedpointmult fixedpointmult_24: pin names not known; wires that end beside it: absunit_29_p2, absunit_29_p2, fixedpointmult_24_p3
  // fixedpointmult fixedpointmult_25: pin names not known; wires that end beside it: absunit_30_p2, absunit_30_p2, fixedpointmult_25_p3, newIMAGE_5
  Multiplexer #(.Bits(16)) multiplexer_11 (
    .sel(newIMAGE_4[15]), .in_0(fixedpointmult_23_p3), .in_1(neg_10_out), .out(newIMAGE_5));
  Add #(.Bits(16)) add_15 (
    .a(fixedpointmult_24_p3), .b(fixedpointmult_25_p3), .c_i(pulldown_17_out), .s(grtrThanFOUR_4));  // open: c_o
  PullDown pulldown_17 (.out(pulldown_17_out));
  // absunit absunit_31: pin names not known; wires that end beside it: newREALS_5, absunit_31_p2
  // absunit absunit_32: pin names not known; wires that end beside it: newREALS_5, absunit_32_p2
  // absunit absunit_33: pin names not known; wires that end beside it: newIMAGE_5, absunit_33_p2
  BarrelShifter #(.barrelShifterMode("arithmetic"), .Bits(16)) arithmetic_shift_6 (
    .in(absunit_31_p2), .shift(5'b00001), .out(arithmetic_shift_6_out));
  Neg #(.Bits(16)) neg_11 (.in(arithmetic_shift_6_out), .out(neg_11_out));
  // fixedpointmult fixedpointmult_26: pin names not known; wires that end beside it: absunit_32_p2, newREALS_5, fixedpointmult_26_p3
  // fixedpointmult fixedpointmult_27: pin names not known; wires that end beside it: absunit_33_p2, fixedpointmult_27_p2
  Multiplexer #(.Bits(16)) multiplexer_12 (
    .sel(newREALS_5[15]), .in_0(arithmetic_shift_6_out), .in_1(neg_11_out), .out(multiplexer_12_out));
  // absunit absunit_34: pin names not known; wires that end beside it: newIMAGE_5, absunit_34_p2
  Sub #(.Bits(16)) sub_6 (
    .a(fixedpointmult_26_p3), .b(fixedpointmult_27_p2), .c_i(pulldown_18_out), .s(sub_6_s));  // open: c_o
  PullDown pulldown_18 (.out(pulldown_18_out));
  Add #(.Bits(16)) add_16 (.a(16'h1000), .b(multiplexer_12_out), .c_i(pulldown_19_out), .s(add_16_s));  // open: c_o
  PullDown pulldown_19 (.out(pulldown_19_out));
  Add #(.Bits(16)) add_17 (.a(newREALS_5), .b(sub_6_s), .c_i(pulldown_18_out), .s(newREALS_6));  // open: c_o
  // absunit absunit_35: pin names not known; wires that end beside it: newREALS_6, absunit_35_p2
  // absunit absunit_36: pin names not known; wires that end beside it: newIMAGE_6, absunit_36_p2
  // fixedpointmult fixedpointmult_28: pin names not known; wires that end beside it: add_16_s, absunit_34_p2, fixedpointmult_28_p3
  Neg #(.Bits(16)) neg_12 (.in(fixedpointmult_28_p3), .out(neg_12_out));
  // fixedpointmult fixedpointmult_29: pin names not known; wires that end beside it: absunit_35_p2, absunit_35_p2, fixedpointmult_29_p3
  // fixedpointmult fixedpointmult_30: pin names not known; wires that end beside it: absunit_36_p2, absunit_36_p2, fixedpointmult_30_p3, newIMAGE_6
  Multiplexer #(.Bits(16)) multiplexer_13 (
    .sel(newIMAGE_5[15]), .in_0(fixedpointmult_28_p3), .in_1(neg_12_out), .out(newIMAGE_6));
  PullDown pulldown_20 (.out(pulldown_20_out));
  Add #(.Bits(16)) add_18 (
    .a(fixedpointmult_29_p3), .b(fixedpointmult_30_p3), .c_i(pulldown_21_out), .s(grtrThanFOUR_6));  // open: c_o
  PullDown pulldown_21 (.out(pulldown_21_out));
  or or_1 (or_1_out, pulldown_20_out, pulldown_20_out, pulldown_20_out, pulldown_20_out, pulldown_20_out, pulldown_20_out, pulldown_20_out, pulldown_20_out, pulldown_20_out, pulldown_20_out, pulldown_20_out, pulldown_20_out, pulldown_20_out, pulldown_20_out, pulldown_20_out, pulldown_20_out, pulldown_20_out, grtrThanFOUR_15[0], grtrThanFOUR_16[0], grtrThanFOUR_14[0], grtrThanFOUR_13[0], grtrThanFOUR_12[0], grtrThanFOUR_11[0], grtrThanFOUR_10[0], grtrThanFOUR_9[0], grtrThanFOUR_8[0], grtrThanFOUR_7[0], grtrThanFOUR_6[0], grtrThanFOUR_4[0], grtrThanFOUR_3[0], grtrThanFOUR_2[0], grtrThanFOUR[0]);
  // absunit absunit_37: pin names not known; wires that end beside it: newREALS_6, absunit_37_p2
  BarrelShifter #(.barrelShifterMode("arithmetic"), .Bits(16)) arithmetic_shift_7 (
    .in(absunit_37_p2), .shift(5'b00001), .out(arithmetic_shift_7_out));
  // absunit absunit_38: pin names not known; wires that end beside it: newREALS_6, absunit_38_p2
  // absunit absunit_39: pin names not known; wires that end beside it: newIMAGE_6, absunit_39_p2
  Neg #(.Bits(16)) neg_13 (.in(arithmetic_shift_7_out), .out(neg_13_out));
  // fixedpointmult fixedpointmult_31: pin names not known; wires that end beside it: absunit_38_p2, newREALS_6, fixedpointmult_31_p3
  // fixedpointmult fixedpointmult_32: pin names not known; wires that end beside it: absunit_39_p2, fixedpointmult_32_p2
  Multiplexer #(.Bits(16)) multiplexer_14 (
    .sel(newREALS_6[15]), .in_0(arithmetic_shift_7_out), .in_1(neg_13_out), .out(multiplexer_14_out));
  // absunit absunit_40: pin names not known; wires that end beside it: newIMAGE_6, absunit_40_p2
  Sub #(.Bits(16)) sub_7 (
    .a(fixedpointmult_31_p3), .b(fixedpointmult_32_p2), .c_i(pulldown_22_out), .s(sub_7_s));  // open: c_o
  PullDown pulldown_22 (.out(pulldown_22_out));
  PullDown pulldown_23 (.out(pulldown_23_out));
  Add #(.Bits(16)) add_19 (.a(16'h1000), .b(multiplexer_14_out), .c_i(pulldown_23_out), .s(add_19_s));  // open: c_o
  Add #(.Bits(16)) add_20 (.a(newREALS_6), .b(sub_7_s), .c_i(pulldown_22_out), .s(newREALS_7));  // open: c_o
  // fixedpointmult fixedpointmult_33: pin names not known; wires that end beside it: add_19_s, absunit_40_p2, fixedpointmult_33_p3
  // absunit absunit_41: pin names not known; wires that end beside it: newREALS_7, absunit_41_p2
  // absunit absunit_42: pin names not known; wires that end beside it: newIMAGE_7, absunit_42_p2
  Neg #(.Bits(16)) neg_14 (.in(fixedpointmult_33_p3), .out(neg_14_out));
  // fixedpointmult fixedpointmult_34: pin names not known; wires that end beside it: absunit_41_p2, absunit_41_p2, fixedpointmult_34_p3
  // fixedpointmult fixedpointmult_35: pin names not known; wires that end beside it: absunit_42_p2, absunit_42_p2, fixedpointmult_35_p3, newIMAGE_7
  Multiplexer #(.Bits(16)) multiplexer_15 (
    .sel(newIMAGE_6[15]), .in_0(fixedpointmult_33_p3), .in_1(neg_14_out), .out(newIMAGE_7));
  Add #(.Bits(16)) add_21 (
    .a(fixedpointmult_34_p3), .b(fixedpointmult_35_p3), .c_i(pulldown_24_out), .s(grtrThanFOUR_7));  // open: c_o
  PullDown pulldown_24 (.out(pulldown_24_out));
  // absunit absunit_43: pin names not known; wires that end beside it: newREALS_7, absunit_43_p2
  BarrelShifter #(.barrelShifterMode("arithmetic"), .Bits(16)) arithmetic_shift_8 (
    .in(absunit_43_p2), .shift(5'b00001), .out(arithmetic_shift_8_out));
  // absunit absunit_44: pin names not known; wires that end beside it: newREALS_7, absunit_44_p2
  // absunit absunit_45: pin names not known; wires that end beside it: newIMAGE_7, absunit_45_p2
  Neg #(.Bits(16)) neg_15 (.in(arithmetic_shift_8_out), .out(neg_15_out));
  // fixedpointmult fixedpointmult_36: pin names not known; wires that end beside it: absunit_44_p2, newREALS_7, fixedpointmult_36_p3
  // fixedpointmult fixedpointmult_37: pin names not known; wires that end beside it: absunit_45_p2, fixedpointmult_37_p2
  Multiplexer #(.Bits(16)) multiplexer_16 (
    .sel(newREALS_7[15]), .in_0(arithmetic_shift_8_out), .in_1(neg_15_out), .out(multiplexer_16_out));
  // absunit absunit_46: pin names not known; wires that end beside it: newIMAGE_7, absunit_46_p2
  Sub #(.Bits(16)) sub_8 (
    .a(fixedpointmult_36_p3), .b(fixedpointmult_37_p2), .c_i(pulldown_25_out), .s(sub_8_s));  // open: c_o
  PullDown pulldown_25 (.out(pulldown_25_out));
  PullDown pulldown_26 (.out(pulldown_26_out));
  Add #(.Bits(16)) add_22 (.a(16'h1000), .b(multiplexer_16_out), .c_i(pulldown_26_out), .s(add_22_s));  // open: c_o
  Add #(.Bits(16)) add_23 (.a(newREALS_7), .b(sub_8_s), .c_i(pulldown_25_out), .s(newREALS_8));  // open: c_o
  // fixedpointmult fixedpointmult_38: pin names not known; wires that end beside it: add_22_s, absunit_46_p2, fixedpointmult_38_p3
  // absunit absunit_47: pin names not known; wires that end beside it: newREALS_8, absunit_47_p2
  // absunit absunit_48: pin names not known; wires that end beside it: newIMAGE_8, absunit_48_p2
  Neg #(.Bits(16)) neg_16 (.in(fixedpointmult_38_p3), .out(neg_16_out));
  // fixedpointmult fixedpointmult_39: pin names not known; wires that end beside it: absunit_47_p2, absunit_47_p2, fixedpointmult_39_p3
  // fixedpointmult fixedpointmult_40: pin names not known; wires that end beside it: absunit_48_p2, absunit_48_p2, fixedpointmult_40_p3
  Multiplexer #(.Bits(16)) multiplexer_17 (
    .sel(newIMAGE_7[15]), .in_0(fixedpointmult_38_p3), .in_1(neg_16_out), .out(newIMAGE_8));
  Add #(.Bits(16)) add_24 (
    .a(fixedpointmult_39_p3), .b(fixedpointmult_40_p3), .c_i(pulldown_27_out), .s(grtrThanFOUR_8));  // open: c_o
  PullDown pulldown_27 (.out(pulldown_27_out));
  // absunit absunit_49: pin names not known; wires that end beside it: newREALS_8, absunit_49_p2
  BarrelShifter #(.barrelShifterMode("arithmetic"), .Bits(16)) arithmetic_shift_9 (
    .in(absunit_49_p2), .shift(5'b00001), .out(arithmetic_shift_9_out));
  // absunit absunit_50: pin names not known; wires that end beside it: newREALS_8, absunit_50_p2
  // absunit absunit_51: pin names not known; wires that end beside it: newIMAGE_8, absunit_51_p2
  Neg #(.Bits(16)) neg_17 (.in(arithmetic_shift_9_out), .out(neg_17_out));
  // fixedpointmult fixedpointmult_41: pin names not known; wires that end beside it: absunit_50_p2, newREALS_8, fixedpointmult_41_p3
  // fixedpointmult fixedpointmult_42: pin names not known; wires that end beside it: absunit_51_p2, fixedpointmult_42_p2
  Multiplexer #(.Bits(16)) multiplexer_18 (
    .sel(newREALS_8[15]), .in_0(arithmetic_shift_9_out), .in_1(neg_17_out), .out(multiplexer_18_out));
  // absunit absunit_52: pin names not known; wires that end beside it: newIMAGE_8, absunit_52_p2
  Sub #(.Bits(16)) sub_9 (
    .a(fixedpointmult_41_p3), .b(fixedpointmult_42_p2), .c_i(pulldown_28_out), .s(sub_9_s));  // open: c_o
  PullDown pulldown_28 (.out(pulldown_28_out));
  PullDown pulldown_29 (.out(pulldown_29_out));
  Add #(.Bits(16)) add_25 (.a(16'h1000), .b(multiplexer_18_out), .c_i(pulldown_29_out), .s(add_25_s));  // open: c_o
  Add #(.Bits(16)) add_26 (.a(newREALS_8), .b(sub_9_s), .c_i(pulldown_28_out), .s(newREALS_9));  // open: c_o
  // fixedpointmult fixedpointmult_43: pin names not known; wires that end beside it: add_25_s, absunit_52_p2, fixedpointmult_43_p3
  // absunit absunit_53: pin names not known; wires that end beside it: newREALS_9, absunit_53_p2
  // absunit absunit_54: pin names not known; wires that end beside it: newIMAGE_9, absunit_54_p2
  Neg #(.Bits(16)) neg_18 (.in(fixedpointmult_43_p3), .out(neg_18_out));
  // fixedpointmult fixedpointmult_44: pin names not known; wires that end beside it: absunit_53_p2, absunit_53_p2, fixedpointmult_44_p3
  // fixedpointmult fixedpointmult_45: pin names not known; wires that end beside it: absunit_54_p2, absunit_54_p2, fixedpointmult_45_p3, newIMAGE_9
  Multiplexer #(.Bits(16)) multiplexer_19 (
    .sel(newIMAGE_8[15]), .in_0(fixedpointmult_43_p3), .in_1(neg_18_out), .out(newIMAGE_9));
  Add #(.Bits(16)) add_27 (
    .a(fixedpointmult_44_p3), .b(fixedpointmult_45_p3), .c_i(pulldown_30_out), .s(grtrThanFOUR_9));  // open: c_o
  PullDown pulldown_30 (.out(pulldown_30_out));
  // absunit absunit_55: pin names not known; wires that end beside it: newREALS_9, absunit_55_p2
  BarrelShifter #(.barrelShifterMode("arithmetic"), .Bits(16)) arithmetic_shift_10 (
    .in(absunit_55_p2), .shift(5'b00001), .out(arithmetic_shift_10_out));
  // absunit absunit_56: pin names not known; wires that end beside it: newREALS_9, absunit_56_p2
  // absunit absunit_57: pin names not known; wires that end beside it: newIMAGE_9, absunit_57_p2
  Neg #(.Bits(16)) neg_19 (.in(arithmetic_shift_10_out), .out(neg_19_out));
  // fixedpointmult fixedpointmult_46: pin names not known; wires that end beside it: absunit_56_p2, newREALS_9, fixedpointmult_46_p3
  // fixedpointmult fixedpointmult_47: pin names not known; wires that end beside it: absunit_57_p2, fixedpointmult_47_p2
  Multiplexer #(.Bits(16)) multiplexer_20 (
    .sel(newREALS_9[15]), .in_0(arithmetic_shift_10_out), .in_1(neg_19_out), .out(multiplexer_20_out));
  // absunit absunit_58: pin names not known; wires that end beside it: newIMAGE_9, absunit_58_p2
  Sub #(.Bits(16)) sub_10 (
    .a(fixedpointmult_46_p3), .b(fixedpointmult_47_p2), .c_i(pulldown_31_out), .s(sub_10_s));  // open: c_o
  PullDown pulldown_31 (.out(pulldown_31_out));
  PullDown pulldown_32 (.out(pulldown_32_out));
  Add #(.Bits(16)) add_28 (.a(16'h1000), .b(multiplexer_20_out), .c_i(pulldown_32_out), .s(add_28_s));  // open: c_o
  Add #(.Bits(16)) add_29 (.a(newREALS_9), .b(sub_10_s), .c_i(pulldown_31_out), .s(newREALS_10));  // open: c_o
  // fixedpointmult fixedpointmult_48: pin names not known; wires that end beside it: add_28_s, absunit_58_p2, fixedpointmult_48_p3
  // absunit absunit_59: pin names not known; wires that end beside it: newREALS_10, absunit_59_p2
  // absunit absunit_60: pin names not known; wires that end beside it: newIMAGE_10, absunit_60_p2
  Neg #(.Bits(16)) neg_20 (.in(fixedpointmult_48_p3), .out(neg_20_out));
  // fixedpointmult fixedpointmult_49: pin names not known; wires that end beside it: absunit_59_p2, absunit_59_p2, fixedpointmult_49_p3
  // fixedpointmult fixedpointmult_50: pin names not known; wires that end beside it: absunit_60_p2, absunit_60_p2, fixedpointmult_50_p3, newIMAGE_10
  Multiplexer #(.Bits(16)) multiplexer_21 (
    .sel(newIMAGE_9[15]), .in_0(fixedpointmult_48_p3), .in_1(neg_20_out), .out(newIMAGE_10));
  Add #(.Bits(16)) add_30 (
    .a(fixedpointmult_49_p3), .b(fixedpointmult_50_p3), .c_i(pulldown_33_out), .s(grtrThanFOUR_10));  // open: c_o
  PullDown pulldown_33 (.out(pulldown_33_out));
  // absunit absunit_61: pin names not known; wires that end beside it: newREALS_10, absunit_61_p2
  // absunit absunit_62: pin names not known; wires that end beside it: newREALS_10, absunit_62_p2
  // absunit absunit_63: pin names not known; wires that end beside it: newIMAGE_10, absunit_63_p2
  BarrelShifter #(.barrelShifterMode("arithmetic"), .Bits(16)) arithmetic_shift_11 (
    .in(absunit_61_p2), .shift(5'b00001), .out(arithmetic_shift_11_out));
  Neg #(.Bits(16)) neg_21 (.in(arithmetic_shift_11_out), .out(neg_21_out));
  // fixedpointmult fixedpointmult_51: pin names not known; wires that end beside it: absunit_62_p2, newREALS_10, fixedpointmult_51_p3
  // fixedpointmult fixedpointmult_52: pin names not known; wires that end beside it: absunit_63_p2, fixedpointmult_52_p2
  Multiplexer #(.Bits(16)) multiplexer_22 (
    .sel(newREALS_10[15]), .in_0(arithmetic_shift_11_out), .in_1(neg_21_out), .out(multiplexer_22_out));
  // absunit absunit_64: pin names not known; wires that end beside it: newIMAGE_10, absunit_64_p2
  Sub #(.Bits(16)) sub_11 (
    .a(fixedpointmult_51_p3), .b(fixedpointmult_52_p2), .c_i(pulldown_34_out), .s(sub_11_s));  // open: c_o
  PullDown pulldown_34 (.out(pulldown_34_out));
  Add #(.Bits(16)) add_31 (.a(16'h1000), .b(multiplexer_22_out), .c_i(pulldown_35_out), .s(add_31_s));  // open: c_o
  PullDown pulldown_35 (.out(pulldown_35_out));
  Add #(.Bits(16)) add_32 (.a(newREALS_10), .b(sub_11_s), .c_i(pulldown_34_out), .s(newREALS_11));  // open: c_o
  // absunit absunit_65: pin names not known; wires that end beside it: newREALS_11, absunit_65_p2
  // absunit absunit_66: pin names not known; wires that end beside it: newIMAGE_11, absunit_66_p2
  // fixedpointmult fixedpointmult_53: pin names not known; wires that end beside it: add_31_s, absunit_64_p2, fixedpointmult_53_p3
  Neg #(.Bits(16)) neg_22 (.in(fixedpointmult_53_p3), .out(neg_22_out));
  // fixedpointmult fixedpointmult_54: pin names not known; wires that end beside it: absunit_65_p2, absunit_65_p2, fixedpointmult_54_p3
  // fixedpointmult fixedpointmult_55: pin names not known; wires that end beside it: absunit_66_p2, absunit_66_p2, fixedpointmult_55_p3, newIMAGE_11
  Multiplexer #(.Bits(16)) multiplexer_23 (
    .sel(newIMAGE_10[15]), .in_0(fixedpointmult_53_p3), .in_1(neg_22_out), .out(newIMAGE_11));
  Add #(.Bits(16)) add_33 (
    .a(fixedpointmult_54_p3), .b(fixedpointmult_55_p3), .c_i(pulldown_36_out), .s(grtrThanFOUR_11));  // open: c_o
  PullDown pulldown_36 (.out(pulldown_36_out));
  // absunit absunit_67: pin names not known; wires that end beside it: newREALS_11, absunit_67_p2
  // absunit absunit_68: pin names not known; wires that end beside it: newREALS_11, absunit_68_p2
  // absunit absunit_69: pin names not known; wires that end beside it: newIMAGE_11, absunit_69_p2
  BarrelShifter #(.barrelShifterMode("arithmetic"), .Bits(16)) arithmetic_shift_12 (
    .in(absunit_67_p2), .shift(5'b00001), .out(arithmetic_shift_12_out));
  Neg #(.Bits(16)) neg_23 (.in(arithmetic_shift_12_out), .out(neg_23_out));
  // fixedpointmult fixedpointmult_56: pin names not known; wires that end beside it: absunit_68_p2, newREALS_11, fixedpointmult_56_p3
  // fixedpointmult fixedpointmult_57: pin names not known; wires that end beside it: absunit_69_p2, fixedpointmult_57_p2
  Multiplexer #(.Bits(16)) multiplexer_24 (
    .sel(newREALS_11[15]), .in_0(arithmetic_shift_12_out), .in_1(neg_23_out), .out(multiplexer_24_out));
  // absunit absunit_70: pin names not known; wires that end beside it: newIMAGE_11, absunit_70_p2
  Sub #(.Bits(16)) sub_12 (
    .a(fixedpointmult_56_p3), .b(fixedpointmult_57_p2), .c_i(pulldown_37_out), .s(sub_12_s));  // open: c_o
  PullDown pulldown_37 (.out(pulldown_37_out));
  Add #(.Bits(16)) add_34 (.a(16'h1000), .b(multiplexer_24_out), .c_i(pulldown_38_out), .s(add_34_s));  // open: c_o
  PullDown pulldown_38 (.out(pulldown_38_out));
  Add #(.Bits(16)) add_35 (.a(newREALS_11), .b(sub_12_s), .c_i(pulldown_37_out), .s(newREALS_12));  // open: c_o
  // absunit absunit_71: pin names not known; wires that end beside it: newREALS_12, absunit_71_p2
  // absunit absunit_72: pin names not known; wires that end beside it: newIMAGE_12, absunit_72_p2
  // fixedpointmult fixedpointmult_58: pin names not known; wires that end beside it: add_34_s, absunit_70_p2, fixedpointmult_58_p3
  Neg #(.Bits(16)) neg_24 (.in(fixedpointmult_58_p3), .out(neg_24_out));
  // fixedpointmult fixedpointmult_59: pin names not known; wires that end beside it: absunit_71_p2, absunit_71_p2, fixedpointmult_59_p3
  // fixedpointmult fixedpointmult_60: pin names not known; wires that end beside it: absunit_72_p2, absunit_72_p2, fixedpointmult_60_p3, newIMAGE_12
  Multiplexer #(.Bits(16)) multiplexer_25 (
    .sel(newIMAGE_11[15]), .in_0(fixedpointmult_58_p3), .in_1(neg_24_out), .out(newIMAGE_12));
  Add #(.Bits(16)) add_36 (
    .a(fixedpointmult_59_p3), .b(fixedpointmult_60_p3), .c_i(pulldown_39_out), .s(grtrThanFOUR_12));  // open: c_o
  PullDown pulldown_39 (.out(pulldown_39_out));
  // absunit absunit_73: pin names not known; wires that end beside it: newREALS_12, newREALS_12, absunit_73_p3
  // absunit absunit_74: pin names not known; wires that end beside it: newREALS_12, absunit_74_p2
  // absunit absunit_75: pin names not known; wires that end beside it: newIMAGE_12, absunit_75_p2
  BarrelShifter #(.barrelShifterMode("arithmetic"), .Bits(16)) arithmetic_shift_13 (
    .in(absunit_73_p3), .shift(5'b00001), .out(arithmetic_shift_13_out));
  Neg #(.Bits(16)) neg_25 (.in(arithmetic_shift_13_out), .out(neg_25_out));
  // fixedpointmult fixedpointmult_61: pin names not known; wires that end beside it: absunit_74_p2, newREALS_12, fixedpointmult_61_p3
  // fixedpointmult fixedpointmult_62: pin names not known; wires that end beside it: absunit_75_p2, fixedpointmult_62_p2
  Multiplexer #(.Bits(16)) multiplexer_26 (
    .sel(newREALS_12[15]), .in_0(arithmetic_shift_13_out), .in_1(neg_25_out), .out(multiplexer_26_out));
  PullDown pulldown_40 (.out(pulldown_40_out));
  // absunit absunit_76: pin names not known; wires that end beside it: newIMAGE_12, absunit_76_p2
  Sub #(.Bits(16)) sub_13 (
    .a(fixedpointmult_61_p3), .b(fixedpointmult_62_p2), .c_i(pulldown_40_out), .s(sub_13_s));  // open: c_o
  Add #(.Bits(16)) add_37 (.a(16'h1000), .b(multiplexer_26_out), .c_i(pulldown_41_out), .s(add_37_s));  // open: c_o
  PullDown pulldown_41 (.out(pulldown_41_out));
  Add #(.Bits(16)) add_38 (.a(newREALS_12), .b(sub_13_s), .c_i(pulldown_40_out), .s(newREALS_13));  // open: c_o
  // fixedpointmult fixedpointmult_63: pin names not known; wires that end beside it: add_37_s, absunit_76_p2, fixedpointmult_63_p3
  // absunit absunit_77: pin names not known; wires that end beside it: newREALS_13, absunit_77_p2
  // absunit absunit_78: pin names not known; wires that end beside it: newIMAGE_13, absunit_78_p2
  Neg #(.Bits(16)) neg_26 (.in(fixedpointmult_63_p3), .out(neg_26_out));
  // fixedpointmult fixedpointmult_64: pin names not known; wires that end beside it: absunit_77_p2, absunit_77_p2, fixedpointmult_64_p3
  // fixedpointmult fixedpointmult_65: pin names not known; wires that end beside it: absunit_78_p2, absunit_78_p2, fixedpointmult_65_p3, newIMAGE_13
  Multiplexer #(.Bits(16)) multiplexer_27 (
    .sel(newIMAGE_12[15]), .in_0(fixedpointmult_63_p3), .in_1(neg_26_out), .out(newIMAGE_13));
  Add #(.Bits(16)) add_39 (
    .a(fixedpointmult_64_p3), .b(fixedpointmult_65_p3), .c_i(pulldown_42_out), .s(grtrThanFOUR_13));  // open: c_o
  PullDown pulldown_42 (.out(pulldown_42_out));
  // absunit absunit_79: pin names not known; wires that end beside it: newREALS_13, absunit_79_p2
  // absunit absunit_80: pin names not known; wires that end beside it: newREALS_13, absunit_80_p2
  // absunit absunit_81: pin names not known; wires that end beside it: newIMAGE_13, absunit_81_p2
  BarrelShifter #(.barrelShifterMode("arithmetic"), .Bits(16)) arithmetic_shift_14 (
    .in(absunit_79_p2), .shift(5'b00001), .out(arithmetic_shift_14_out));
  Neg #(.Bits(16)) neg_27 (.in(arithmetic_shift_14_out), .out(neg_27_out));
  // fixedpointmult fixedpointmult_66: pin names not known; wires that end beside it: absunit_80_p2, newREALS_13, fixedpointmult_66_p3
  // fixedpointmult fixedpointmult_67: pin names not known; wires that end beside it: absunit_81_p2, fixedpointmult_67_p2
  Multiplexer #(.Bits(16)) multiplexer_28 (
    .sel(newREALS_13[15]), .in_0(arithmetic_shift_14_out), .in_1(neg_27_out), .out(multiplexer_28_out));
  PullDown pulldown_43 (.out(pulldown_43_out));
  // absunit absunit_82: pin names not known; wires that end beside it: newIMAGE_13, absunit_82_p2
  Sub #(.Bits(16)) sub_14 (
    .a(fixedpointmult_66_p3), .b(fixedpointmult_67_p2), .c_i(pulldown_43_out), .s(sub_14_s));  // open: c_o
  Add #(.Bits(16)) add_40 (.a(16'h1000), .b(multiplexer_28_out), .c_i(pulldown_44_out), .s(add_40_s));  // open: c_o
  PullDown pulldown_44 (.out(pulldown_44_out));
  Add #(.Bits(16)) add_41 (.a(newREALS_13), .b(sub_14_s), .c_i(pulldown_43_out), .s(newREALS_14));  // open: c_o
  // fixedpointmult fixedpointmult_68: pin names not known; wires that end beside it: add_40_s, absunit_82_p2, fixedpointmult_68_p3
  // absunit absunit_83: pin names not known; wires that end beside it: newREALS_14, absunit_83_p2
  // absunit absunit_84: pin names not known; wires that end beside it: newIMAGE_14, absunit_84_p2
  Neg #(.Bits(16)) neg_28 (.in(fixedpointmult_68_p3), .out(neg_28_out));
  // fixedpointmult fixedpointmult_69: pin names not known; wires that end beside it: absunit_83_p2, absunit_83_p2, fixedpointmult_69_p3
  // fixedpointmult fixedpointmult_70: pin names not known; wires that end beside it: absunit_84_p2, absunit_84_p2, fixedpointmult_70_p3, newIMAGE_14
  Multiplexer #(.Bits(16)) multiplexer_29 (
    .sel(newIMAGE_13[15]), .in_0(fixedpointmult_68_p3), .in_1(neg_28_out), .out(newIMAGE_14));
  Add #(.Bits(16)) add_42 (
    .a(fixedpointmult_69_p3), .b(fixedpointmult_70_p3), .c_i(pulldown_45_out), .s(grtrThanFOUR_14));  // open: c_o
  PullDown pulldown_45 (.out(pulldown_45_out));
  // absunit absunit_85: pin names not known; wires that end beside it: newREALS_14, absunit_85_p2
  BarrelShifter #(.barrelShifterMode("arithmetic"), .Bits(16)) arithmetic_shift_15 (
    .in(absunit_85_p2), .shift(5'b00001), .out(arithmetic_shift_15_out));
  // absunit absunit_86: pin names not known; wires that end beside it: newREALS_14, absunit_86_p2
  // absunit absunit_87: pin names not known; wires that end beside it: newIMAGE_14, absunit_87_p2
  Neg #(.Bits(16)) neg_29 (.in(arithmetic_shift_15_out), .out(neg_29_out));
  // fixedpointmult fixedpointmult_71: pin names not known; wires that end beside it: absunit_86_p2, newREALS_14, fixedpointmult_71_p3
  // fixedpointmult fixedpointmult_72: pin names not known; wires that end beside it: absunit_87_p2, fixedpointmult_72_p2
  Multiplexer #(.Bits(16)) multiplexer_30 (
    .sel(newREALS_14[15]), .in_0(arithmetic_shift_15_out), .in_1(neg_29_out), .out(multiplexer_30_out));
  // absunit absunit_88: pin names not known; wires that end beside it: newIMAGE_14, absunit_88_p2
  Sub #(.Bits(16)) sub_15 (
    .a(fixedpointmult_71_p3), .b(fixedpointmult_72_p2), .c_i(pulldown_46_out), .s(sub_15_s));  // open: c_o
  PullDown pulldown_46 (.out(pulldown_46_out));
  Add #(.Bits(16)) add_43 (.a(16'h1000), .b(multiplexer_30_out), .c_i(pulldown_47_out), .s(add_43_s));  // open: c_o
  PullDown pulldown_47 (.out(pulldown_47_out));
  Add #(.Bits(16)) add_44 (.a(newREALS_14), .b(sub_15_s), .c_i(pulldown_46_out), .s(newREALS_15));  // open: c_o
  // absunit absunit_89: pin names not known; wires that end beside it: newREALS_15, absunit_89_p2
  // absunit absunit_90: pin names not known; wires that end beside it: newIMAGE_15, absunit_90_p2
  // fixedpointmult fixedpointmult_73: pin names not known; wires that end beside it: add_43_s, absunit_88_p2, fixedpointmult_73_p3
  // fixedpointmult fixedpointmult_74: pin names not known; wires that end beside it: absunit_89_p2, absunit_89_p2, fixedpointmult_74_p3
  // fixedpointmult fixedpointmult_75: pin names not known; wires that end beside it: absunit_90_p2, absunit_90_p2, fixedpointmult_75_p3, newIMAGE_15
  Neg #(.Bits(16)) neg_30 (.in(fixedpointmult_73_p3), .out(neg_30_out));
  Multiplexer #(.Bits(16)) multiplexer_31 (
    .sel(newIMAGE_14[15]), .in_0(fixedpointmult_73_p3), .in_1(neg_30_out), .out(newIMAGE_15));
  PullDown pulldown_48 (.out(pulldown_48_out));
  Add #(.Bits(16)) add_45 (
    .a(fixedpointmult_74_p3), .b(fixedpointmult_75_p3), .c_i(pulldown_48_out), .s(grtrThanFOUR_15));  // open: c_o
  // absunit absunit_91: pin names not known; wires that end beside it: newREALS_15, absunit_91_p2
  BarrelShifter #(.barrelShifterMode("arithmetic"), .Bits(16)) arithmetic_shift_16 (
    .in(absunit_91_p2), .shift(5'b00001), .out(arithmetic_shift_16_out));
  // absunit absunit_92: pin names not known; wires that end beside it: newREALS_15, absunit_92_p2
  // absunit absunit_93: pin names not known; wires that end beside it: newIMAGE_15, absunit_93_p2
  Neg #(.Bits(16)) neg_31 (.in(arithmetic_shift_16_out), .out(neg_31_out));
  // fixedpointmult fixedpointmult_76: pin names not known; wires that end beside it: absunit_92_p2, newREALS_15, fixedpointmult_76_p3
  // fixedpointmult fixedpointmult_77: pin names not known; wires that end beside it: absunit_93_p2, fixedpointmult_77_p2
  Multiplexer #(.Bits(16)) multiplexer_32 (
    .sel(newREALS_15[15]), .in_0(arithmetic_shift_16_out), .in_1(neg_31_out), .out(multiplexer_32_out));
  // absunit absunit_94: pin names not known; wires that end beside it: newIMAGE_15, absunit_94_p2
  Sub #(.Bits(16)) sub_16 (
    .a(fixedpointmult_76_p3), .b(fixedpointmult_77_p2), .c_i(pulldown_49_out), .s(sub_16_s));  // open: c_o
  PullDown pulldown_49 (.out(pulldown_49_out));
  Add #(.Bits(16)) add_46 (.a(16'h1000), .b(multiplexer_32_out), .c_i(pulldown_50_out), .s(add_46_s));  // open: c_o
  PullDown pulldown_50 (.out(pulldown_50_out));
  Add #(.Bits(16)) add_47 (.a(newREALS_15), .b(sub_16_s), .c_i(pulldown_49_out), .s(newREALS_16));  // open: c_o
  // absunit absunit_95: pin names not known; wires that end beside it: newREALS_16, absunit_95_p2
  // absunit absunit_96: pin names not known; wires that end beside it: newIMAGE_16, absunit_96_p2
  // fixedpointmult fixedpointmult_78: pin names not known; wires that end beside it: add_46_s, absunit_94_p2, fixedpointmult_78_p3
  // fixedpointmult fixedpointmult_79: pin names not known; wires that end beside it: absunit_95_p2, absunit_95_p2, fixedpointmult_79_p3
  // fixedpointmult fixedpointmult_80: pin names not known; wires that end beside it: absunit_96_p2, absunit_96_p2, fixedpointmult_80_p3, newIMAGE_16
  Neg #(.Bits(16)) neg_32 (.in(fixedpointmult_78_p3), .out(neg_32_out));
  Multiplexer #(.Bits(16)) multiplexer_33 (
    .sel(newIMAGE_15[15]), .in_0(fixedpointmult_78_p3), .in_1(neg_32_out), .out(newIMAGE_16));
  PullDown pulldown_51 (.out(pulldown_51_out));
  Add #(.Bits(16)) add_48 (
    .a(fixedpointmult_79_p3), .b(fixedpointmult_80_p3), .c_i(pulldown_51_out), .s(grtrThanFOUR_16));  // open: c_o
  // Pins of 1 and 16 bits meet at grtrThanFOUR
  // Pins of 1 and 16 bits meet at grtrThanFOUR_2
  // Pins of 1 and 16 bits meet at grtrThanFOUR_3
  // Pins of 1 and 16 bits meet at grtrThanFOUR_4
  // Pins of 1 and 16 bits meet at grtrThanFOUR_6
  // Pins of 1 and 16 bits meet at grtrThanFOUR_7
  // Pins of 1 and 16 bits meet at grtrThanFOUR_8
  // Pins of 1 and 16 bits meet at grtrThanFOUR_9
  // Pins of 1 and 16 bits meet at grtrThanFOUR_10
  // Pins of 1 and 16 bits meet at grtrThanFOUR_11
  // Pins of 1 and 16 bits meet at grtrThanFOUR_12
  // Pins of 1 and 16 bits meet at grtrThanFOUR_13

  assign grtrThanFOUR_5 = grtrThanFOUR_4;

  // Notes on the sheet:
  //   clk: Hz: 200
  //   a
  //   a^2
  //   b^2
  //   real = a^2 - b^2 + a
  //   a^3
  //   b^3
  //   a^4
  //   b^4
  //   a^5
  //   b^5
  //   a^6
  //   b^6
  //   a^7
  //   b^7
  //   a^8
  //   b^8
  //   a^9
  //   b^9
  //   a^10
  //   b^10
  //   a^11
  //   b^11
  //   a^12
  //   b^12
  //   a^13
  //   b^13
  //   a^14
  //   b^14
  //   a^15
  //   b^15
  //   a^16
  //   b^16
  //   a^17
  //   b^17
endmodule
