// Digital circuit MANDELBROT.dig as structural Verilog
module MANDELBROT (
  input  in_1,
  input  in_2,
  input  in_3,
  input  in_4,
  input  clk,
  output [4:0] grey
);

  wire nor_1_out, signedcomplex_1_p5, signedcomplex_1_p6, signedcomplex_1_p7, signedcomplex_2_p5,
       signedcomplex_2_p6, signedcomplex_2_p7, signedcomplex_3_p5, signedcomplex_3_p6, signedcomplex_3_p7,
       signedcomplex_4_p5, signedcomplex_4_p6, signedcomplex_4_p7, signedcomplex_5_p5, signedcomplex_5_p6,
       signedcomplex_5_p7, signedcomplex_6_p5, signedcomplex_6_p6, signedcomplex_6_p7, signedcomplex_7_p5,
       signedcomplex_7_p6, signedcomplex_7_p7, signedcomplex_8_p5, signedcomplex_8_p6, signedcomplex_8_p7,
       signedcomplex_9_p5, signedcomplex_9_p6, signedcomplex_9_p7, signedcomplex_10_p5, signedcomplex_10_p6,
       signedcomplex_10_p7, signedcomplex_11_p5, signedcomplex_11_p6, signedcomplex_11_p7,
       signedcomplex_12_p5, signedcomplex_12_p6, signedcomplex_12_p7, signedcomplex_13_p5,
       signedcomplex_13_p6, signedcomplex_13_p7, signedcomplex_14_p5, signedcomplex_14_p6,
       signedcomplex_14_p7, signedcomplex_15_p5, signedcomplex_15_p6, signedcomplex_15_p7,
       signedcomplex_16_p5;
  wire [4:0] multiplexer_1_out, multiplexer_2_out, multiplexer_3_out, multiplexer_4_out, multiplexer_5_out,
       multiplexer_6_out, multiplexer_7_out, multiplexer_8_out, multiplexer_9_out, multiplexer_10_out,
       multiplexer_11_out, multiplexer_12_out, multiplexer_13_out, multiplexer_14_out, multiplexer_15_out,
       multiplexer_16_out, multiplexer_17_out;
  wire [6:0] newscreenmap128_1_xcoord;
  wire [7:0] newscreenmap128_1_ycoord;
  wire [7:7] newscreenmap128_1_xcoord_2, not_1_out_2;
  wire [13:7] not_1_out;
  wire [15:0] newscreenmap128_1_mapimage, newscreenmap128_1_mapreal;
  wire [15:15] graphiccard_1_d;

  NEWscreenMAP128 newscreenmap128_1 (
    .mapREAL(newscreenmap128_1_mapreal), .mapIMAGE(newscreenmap128_1_mapimage), .ResetToNeg2(in_3),
    .Xcoord({newscreenmap128_1_xcoord_2[7], newscreenmap128_1_xcoord}), .clock(clk), .enable(in_4),
    .Ycoord(newscreenmap128_1_ycoord));
  assign {not_1_out_2[7], not_1_out} = ~newscreenmap128_1_ycoord;  // Not not_1, 8 bits wide
  // signedCOMPLEX signedcomplex_1: pin names not known; wires that end beside it: newscreenmap128_1_mapreal, newscreenmap128_1_mapimage, newscreenmap128_1_mapimage, newscreenmap128_1_mapreal, signedcomplex_1_p5, signedcomplex_1_p6, signedcomplex_1_p7
  GraphicCard #(.graphicHeight(128), .graphicWidth(128), .Bits(16)) graphiccard_1 (
    .A({1'b0, not_1_out, newscreenmap128_1_xcoord}), .str(in_4), .C(clk), .ld(in_1), .B(in_2),
    .D({graphiccard_1_d[15], grey, grey, grey}));
  // signedCOMPLEX signedcomplex_2: pin names not known; wires that end beside it: signedcomplex_1_p5, signedcomplex_1_p7, newscreenmap128_1_mapimage, newscreenmap128_1_mapreal, signedcomplex_2_p5, signedcomplex_2_p6, signedcomplex_2_p7
  Multiplexer #(.Bits(5)) multiplexer_1 (
    .sel(signedcomplex_1_p6), .in_0({5{1'b0}}), .in_1({5{1'b1}}), .out(multiplexer_1_out));
  // signedCOMPLEX signedcomplex_3: pin names not known; wires that end beside it: signedcomplex_2_p5, signedcomplex_2_p7, newscreenmap128_1_mapimage, newscreenmap128_1_mapreal, signedcomplex_3_p5, signedcomplex_3_p6, signedcomplex_3_p7
  Multiplexer #(.Bits(5)) multiplexer_2 (
    .sel(signedcomplex_2_p6), .in_0({5{1'b0}}), .in_1(5'b11101), .out(multiplexer_2_out));
  // signedCOMPLEX signedcomplex_4: pin names not known; wires that end beside it: signedcomplex_3_p5, signedcomplex_3_p7, newscreenmap128_1_mapimage, newscreenmap128_1_mapreal, signedcomplex_4_p5, signedcomplex_4_p6, signedcomplex_4_p7
  Multiplexer #(.Bits(5)) multiplexer_3 (
    .sel(signedcomplex_3_p6), .in_0({5{1'b0}}), .in_1(5'b11011), .out(multiplexer_3_out));
  // signedCOMPLEX signedcomplex_5: pin names not known; wires that end beside it: signedcomplex_4_p5, signedcomplex_4_p7, newscreenmap128_1_mapimage, newscreenmap128_1_mapreal, signedcomplex_5_p5, signedcomplex_5_p6, signedcomplex_5_p7
  Multiplexer #(.Bits(5)) multiplexer_4 (
    .sel(signedcomplex_4_p6), .in_0({5{1'b0}}), .in_1(5'b11001), .out(multiplexer_4_out));
  // signedCOMPLEX signedcomplex_6: pin names not known; wires that end beside it: signedcomplex_5_p5, signedcomplex_5_p7, newscreenmap128_1_mapimage, newscreenmap128_1_mapreal, signedcomplex_6_p5, signedcomplex_6_p6, signedcomplex_6_p7
  Multiplexer #(.Bits(5)) multiplexer_5 (
    .sel(signedcomplex_5_p6), .in_0({5{1'b0}}), .in_1(5'b10111), .out(multiplexer_5_out));
  // signedCOMPLEX signedcomplex_7: pin names not known; wires that end beside it: signedcomplex_6_p5, signedcomplex_6_p7, newscreenmap128_1_mapimage, newscreenmap128_1_mapreal, signedcomplex_7_p5, signedcomplex_7_p6, signedcomplex_7_p7
  Multiplexer #(.Bits(5)) multiplexer_6 (
    .sel(signedcomplex_6_p6), .in_0({5{1'b0}}), .in_1(5'b10101), .out(multiplexer_6_out));
  nor nor_1 (nor_1_out, signedcomplex_1_p6, signedcomplex_2_p6, signedcomplex_3_p6, signedcomplex_4_p6, signedcomplex_5_p6, signedcomplex_6_p6, signedcomplex_7_p6, signedcomplex_8_p6, signedcomplex_9_p6, signedcomplex_10_p6, signedcomplex_11_p6, signedcomplex_12_p6, signedcomplex_13_p6, signedcomplex_14_p6, signedcomplex_15_p6, signedcomplex_16_p5);
  // signedCOMPLEX signedcomplex_8: pin names not known; wires that end beside it: signedcomplex_7_p5, signedcomplex_7_p7, newscreenmap128_1_mapimage, newscreenmap128_1_mapreal, signedcomplex_8_p5, signedcomplex_8_p6, signedcomplex_8_p7
  Multiplexer #(.Bits(5)) multiplexer_7 (
    .sel(signedcomplex_7_p6), .in_0({5{1'b0}}), .in_1(5'b10011), .out(multiplexer_7_out));
  // signedCOMPLEX signedcomplex_9: pin names not known; wires that end beside it: signedcomplex_8_p5, signedcomplex_8_p7, newscreenmap128_1_mapimage, newscreenmap128_1_mapreal, signedcomplex_9_p5, signedcomplex_9_p6, signedcomplex_9_p7
  Multiplexer #(.Bits(5)) multiplexer_8 (
    .sel(signedcomplex_8_p6), .in_0({5{1'b0}}), .in_1(5'b10001), .out(multiplexer_8_out));
  // signedCOMPLEX signedcomplex_10: pin names not known; wires that end beside it: signedcomplex_9_p5, signedcomplex_9_p7, newscreenmap128_1_mapimage, newscreenmap128_1_mapreal, signedcomplex_10_p5, signedcomplex_10_p6, signedcomplex_10_p7
  Multiplexer #(.Bits(5)) multiplexer_9 (
    .sel(signedcomplex_9_p6), .in_0({5{1'b0}}), .in_1(5'b01111), .out(multiplexer_9_out));
  // signedCOMPLEX signedcomplex_11: pin names not known; wires that end beside it: signedcomplex_10_p5, signedcomplex_10_p7, newscreenmap128_1_mapimage, newscreenmap128_1_mapreal, signedcomplex_11_p5, signedcomplex_11_p6, signedcomplex_11_p7
  Multiplexer #(.Bits(5)) multiplexer_10 (
    .sel(signedcomplex_10_p6), .in_0({5{1'b0}}), .in_1(5'b01101), .out(multiplexer_10_out));
  assign grey = multiplexer_17_out | multiplexer_16_out | multiplexer_15_out | multiplexer_14_out | multiplexer_13_out | multiplexer_12_out | multiplexer_11_out | multiplexer_10_out | multiplexer_9_out | multiplexer_8_out | multiplexer_7_out | multiplexer_6_out | multiplexer_5_out | multiplexer_4_out | multiplexer_3_out | multiplexer_2_out | multiplexer_1_out;  // Or or_1, 5 bits wide
  // signedCOMPLEX signedcomplex_12: pin names not known; wires that end beside it: signedcomplex_11_p5, signedcomplex_11_p7, newscreenmap128_1_mapimage, newscreenmap128_1_mapreal, signedcomplex_12_p5, signedcomplex_12_p6, signedcomplex_12_p7
  Multiplexer #(.Bits(5)) multiplexer_11 (
    .sel(signedcomplex_11_p6), .in_0({5{1'b0}}), .in_1(5'b01011), .out(multiplexer_11_out));
  // signedCOMPLEX signedcomplex_13: pin names not known; wires that end beside it: signedcomplex_12_p5, signedcomplex_12_p7, newscreenmap128_1_mapimage, newscreenmap128_1_mapreal, signedcomplex_13_p5, signedcomplex_13_p6, signedcomplex_13_p7
  Multiplexer #(.Bits(5)) multiplexer_12 (
    .sel(signedcomplex_12_p6), .in_0({5{1'b0}}), .in_1(5'b01001), .out(multiplexer_12_out));
  // signedCOMPLEX signedcomplex_14: pin names not known; wires that end beside it: signedcomplex_13_p5, signedcomplex_13_p7, newscreenmap128_1_mapimage, newscreenmap128_1_mapreal, signedcomplex_14_p5, signedcomplex_14_p6, signedcomplex_14_p7
  Multiplexer #(.Bits(5)) multiplexer_13 (
    .sel(signedcomplex_13_p6), .in_0({5{1'b0}}), .in_1(5'b00111), .out(multiplexer_13_out));
  // signedCOMPLEX signedcomplex_15: pin names not known; wires that end beside it: signedcomplex_14_p5, signedcomplex_14_p7, newscreenmap128_1_mapimage, newscreenmap128_1_mapreal, signedcomplex_15_p5, signedcomplex_15_p6, signedcomplex_15_p7
  Multiplexer #(.Bits(5)) multiplexer_14 (
    .sel(signedcomplex_14_p6), .in_0({5{1'b0}}), .in_1(5'b00101), .out(multiplexer_14_out));
  // signedCOMPLEX signedcomplex_16: pin names not known; wires that end beside it: signedcomplex_15_p5, signedcomplex_15_p7, newscreenmap128_1_mapimage, newscreenmap128_1_mapreal, signedcomplex_16_p5
  Multiplexer #(.Bits(5)) multiplexer_15 (
    .sel(signedcomplex_15_p6), .in_0({5{1'b0}}), .in_1(5'b00011), .out(multiplexer_15_out));
  Multiplexer #(.Bits(5)) multiplexer_16 (
    .sel(signedcomplex_16_p5), .in_0({5{1'b0}}), .in_1(5'b00001), .out(multiplexer_16_out));
  Multiplexer #(.Bits(5)) multiplexer_17 (
    .sel(nor_1_out), .in_0({5{1'b0}}), .in_1({5{1'b0}}), .out(multiplexer_17_out));
  // also tied to VCC on the sheet: graphiccard_1_d[15]

  // Notes on the sheet:
  //   clk: Hz: 5000
endmodule
