// Digital circuit NEWscreenMAP128.dig as structural Verilog
module NEWscreenMAP128 (
  input  ResetToNeg2,
  input  clock,
  input  enable,
  output [15:0] mapREAL,
  output [15:0] mapIMAGE,
  output [7:0] Xcoord,
  output [7:0] Ycoord
);

  wire and_1_out, and_2_out, and_3_out, comparator_1_eq, comparator_2_eq, counter_1_ovf, counter_2_ovf,
       or_1_out, or_2_out, or_3_out, or_4_out, or_5_out, or_6_out, pulldown_1_out, pulldown_2_out;
  wire [15:0] add_1_s, add_2_s, multiplexer_1_out, multiplexer_2_out;

  or or_1 (or_1_out, enable, ResetToNeg2);
  and and_1 (and_1_out, clock, ResetToNeg2);
  or or_2 (or_2_out, comparator_2_eq, ResetToNeg2);
  and and_2 (and_2_out, comparator_1_eq, comparator_2_eq);
  or or_3 (or_3_out, ResetToNeg2, comparator_2_eq);
  Multiplexer #(.Bits(16)) multiplexer_1 (.sel(or_2_out), .in_0(add_2_s), .in_1(16'he000), .out(multiplexer_1_out));
  and and_3 (and_3_out, clock, ~and_2_out);  // And
  or or_4 (or_4_out, and_3_out, and_1_out);
  or or_5 (or_5_out, comparator_1_eq, ResetToNeg2);
  Multiplexer #(.Bits(16)) multiplexer_2 (.sel(or_5_out), .in_0(add_1_s), .in_1(16'he000), .out(multiplexer_2_out));
  or or_6 (or_6_out, comparator_2_eq, ResetToNeg2);
  Counter #(.Bits(8)) counter_1 (.en(or_1_out), .C(or_4_out), .clr(or_3_out), .out(Xcoord), .ovf(counter_1_ovf));
  Register #(.Bits(16)) register_1 (.D(multiplexer_1_out), .C(or_4_out), .en(or_1_out), .Q(mapREAL));
  Register #(.Bits(16)) register_2 (.D(multiplexer_2_out), .C(or_4_out), .en(or_6_out), .Q(mapIMAGE));
  Counter #(.Bits(8)) counter_2 (.en(or_6_out), .C(or_4_out), .clr(ResetToNeg2), .out(Ycoord), .ovf(counter_2_ovf));
  Add #(.Bits(16)) add_1 (.a(mapIMAGE), .b(16'h80), .c_i(1'b0), .s(add_1_s));  // open: c_o
  Add #(.Bits(16)) add_2 (.a(mapREAL), .b(16'h80), .c_i(1'b0), .s(add_2_s));  // open: c_o
  Comparator #(.Bits(16)) comparator_1 (.a(16'h1f80), .b(mapIMAGE), .eq(comparator_1_eq));  // open: gt, lt
  Comparator #(.Bits(16)) comparator_2 (.a(16'h1f80), .b(mapREAL), .eq(comparator_2_eq));  // open: gt, lt
  Seven_Seg_Hex seven_seg_hex_1 (.d(mapREAL[15:12]), .dp(pulldown_2_out));
  Seven_Seg_Hex seven_seg_hex_2 (.d(mapIMAGE[15:12]), .dp(pulldown_1_out));
  Seven_Seg_Hex seven_seg_hex_3 (.d(mapREAL[11:8]), .dp(pulldown_2_out));
  Seven_Seg_Hex seven_seg_hex_4 (.d(mapIMAGE[11:8]), .dp(pulldown_1_out));
  Seven_Seg_Hex seven_seg_hex_5 (.d(mapREAL[7:4]), .dp(pulldown_2_out));
  Seven_Seg_Hex seven_seg_hex_6 (.d(mapIMAGE[7:4]), .dp(pulldown_1_out));
  Seven_Seg_Hex seven_seg_hex_7 (.d(mapREAL[3:0]), .dp(pulldown_2_out));
  Seven_Seg_Hex seven_seg_hex_8 (.d(mapIMAGE[3:0]), .dp(pulldown_1_out));
  PullDown pulldown_1 (.out(pulldown_1_out));
  PullDown pulldown_2 (.out(pulldown_2_out));
endmodule
