// Digital circuit iterations.dig as structural Verilog
module iterations (
  input  [15:0] a,
  input  [15:0] b,
  output [4:0] grey
);

  wire nor_1_out, signedcomplex_1_p3, signedcomplex_1_p4, signedcomplex_1_p5, signedcomplex_2_p3,
       signedcomplex_2_p4, signedcomplex_2_p5, signedcomplex_3_p3, signedcomplex_3_p4, signedcomplex_3_p5,
       signedcomplex_4_p3, signedcomplex_4_p4, signedcomplex_4_p5, signedcomplex_5_p3, signedcomplex_5_p4,
       signedcomplex_5_p5, signedcomplex_6_p3, signedcomplex_6_p4, signedcomplex_6_p5, signedcomplex_7_p3,
       signedcomplex_7_p4, signedcomplex_7_p5, signedcomplex_8_p3, signedcomplex_8_p4, signedcomplex_8_p5,
       signedcomplex_9_p3, signedcomplex_9_p4, signedcomplex_9_p5, signedcomplex_10_p3, signedcomplex_10_p4,
       signedcomplex_10_p5, signedcomplex_11_p3, signedcomplex_11_p4, signedcomplex_11_p5,
       signedcomplex_12_p3, signedcomplex_12_p4, signedcomplex_12_p5, signedcomplex_13_p3,
       signedcomplex_13_p4, signedcomplex_13_p5, signedcomplex_14_p3, signedcomplex_14_p4,
       signedcomplex_14_p5, signedcomplex_15_p3, signedcomplex_15_p4, signedcomplex_15_p5,
       signedcomplex_16_p3;
  wire [4:0] multiplexer_1_out, multiplexer_2_out, multiplexer_3_out, multiplexer_4_out, multiplexer_5_out,
       multiplexer_6_out, multiplexer_7_out, multiplexer_8_out, multiplexer_9_out, multiplexer_10_out,
       multiplexer_11_out, multiplexer_12_out, multiplexer_13_out, multiplexer_14_out, multiplexer_15_out,
       multiplexer_16_out, multiplexer_17_out;

  // signedCOMPLEX signedcomplex_1: pin names not known; wires that end beside it: a, b, signedcomplex_1_p3, signedcomplex_1_p4, signedcomplex_1_p5
  // signedCOMPLEX signedcomplex_2: pin names not known; wires that end beside it: signedcomplex_1_p3, signedcomplex_1_p5, signedcomplex_2_p3, signedcomplex_2_p4, signedcomplex_2_p5
  Multiplexer #(.Bits(5)) multiplexer_1 (
    .sel(signedcomplex_1_p4), .in_0({5{1'b0}}), .in_1({5{1'b1}}), .out(multiplexer_1_out));
  // signedCOMPLEX signedcomplex_3: pin names not known; wires that end beside it: signedcomplex_2_p3, signedcomplex_2_p5, signedcomplex_3_p3, signedcomplex_3_p4, signedcomplex_3_p5
  Multiplexer #(.Bits(5)) multiplexer_2 (
    .sel(signedcomplex_2_p4), .in_0({5{1'b0}}), .in_1(5'b11101), .out(multiplexer_2_out));
  // signedCOMPLEX signedcomplex_4: pin names not known; wires that end beside it: signedcomplex_3_p3, signedcomplex_3_p5, signedcomplex_4_p3, signedcomplex_4_p4, signedcomplex_4_p5
  Multiplexer #(.Bits(5)) multiplexer_3 (
    .sel(signedcomplex_3_p4), .in_0({5{1'b0}}), .in_1(5'b11011), .out(multiplexer_3_out));
  // signedCOMPLEX signedcomplex_5: pin names not known; wires that end beside it: signedcomplex_4_p3, signedcomplex_4_p5, signedcomplex_5_p3, signedcomplex_5_p4, signedcomplex_5_p5
  Multiplexer #(.Bits(5)) multiplexer_4 (
    .sel(signedcomplex_4_p4), .in_0({5{1'b0}}), .in_1(5'b11001), .out(multiplexer_4_out));
  // signedCOMPLEX signedcomplex_6: pin names not known; wires that end beside it: signedcomplex_5_p3, signedcomplex_5_p5, signedcomplex_6_p3, signedcomplex_6_p4, signedcomplex_6_p5
  Multiplexer #(.Bits(5)) multiplexer_5 (
    .sel(signedcomplex_5_p4), .in_0({5{1'b0}}), .in_1(5'b10111), .out(multiplexer_5_out));
  // signedCOMPLEX signedcomplex_7: pin names not known; wires that end beside it: signedcomplex_6_p3, signedcomplex_6_p5, signedcomplex_7_p3, signedcomplex_7_p4, signedcomplex_7_p5
  Multiplexer #(.Bits(5)) multiplexer_6 (
    .sel(signedcomplex_6_p4), .in_0({5{1'b0}}), .in_1(5'b10101), .out(multiplexer_6_out));
  nor nor_1 (nor_1_out, signedcomplex_1_p4, signedcomplex_2_p4, signedcomplex_3_p4, signedcomplex_4_p4, signedcomplex_5_p4, signedcomplex_6_p4, signedcomplex_7_p4, signedcomplex_8_p4, signedcomplex_9_p4, signedcomplex_10_p4, signedcomplex_11_p4, signedcomplex_12_p4, signedcomplex_13_p4, signedcomplex_14_p4, signedcomplex_15_p4, signedcomplex_16_p3);
  // signedCOMPLEX signedcomplex_8: pin names not known; wires that end beside it: signedcomplex_7_p3, signedcomplex_7_p5, signedcomplex_8_p3, signedcomplex_8_p4, signedcomplex_8_p5
  Multiplexer #(.Bits(5)) multiplexer_7 (
    .sel(signedcomplex_7_p4), .in_0({5{1'b0}}), .in_1(5'b10011), .out(multiplexer_7_out));
  // signedCOMPLEX signedcomplex_9: pin names not known; wires that end beside it: signedcomplex_8_p3, signedcomplex_8_p5, signedcomplex_9_p3, signedcomplex_9_p4, signedcomplex_9_p5
  Multiplexer #(.Bits(5)) multiplexer_8 (
    .sel(signedcomplex_8_p4), .in_0({5{1'b0}}), .in_1(5'b10001), .out(multiplexer_8_out));
  // signedCOMPLEX signedcomplex_10: pin names not known; wires that end beside it: signedcomplex_9_p3, signedcomplex_9_p5, signedcomplex_10_p3, signedcomplex_10_p4, signedcomplex_10_p5
  Multiplexer #(.Bits(5)) multiplexer_9 (
    .sel(signedcomplex_9_p4), .in_0({5{1'b0}}), .in_1(5'b01111), .out(multiplexer_9_out));
  // signedCOMPLEX signedcomplex_11: pin names not known; wires that end beside it: signedcomplex_10_p3, signedcomplex_10_p5, signedcomplex_11_p3, signedcomplex_11_p4, signedcomplex_11_p5
  Multiplexer #(.Bits(5)) multiplexer_10 (
    .sel(signedcomplex_10_p4), .in_0({5{1'b0}}), .in_1(5'b01101), .out(multiplexer_10_out));
  assign grey = multiplexer_17_out | multiplexer_16_out | multiplexer_15_out | multiplexer_14_out | multiplexer_13_out | multiplexer_12_out | multiplexer_11_out | multiplexer_10_out | multiplexer_9_out | multiplexer_8_out | multiplexer_7_out | multiplexer_6_out | multiplexer_5_out | multiplexer_4_out | multiplexer_3_out | multiplexer_2_out | multiplexer_1_out;  // Or or_1, 5 bits wide
  // signedCOMPLEX signedcomplex_12: pin names not known; wires that end beside it: signedcomplex_11_p3, signedcomplex_11_p5, signedcomplex_12_p3, signedcomplex_12_p4, signedcomplex_12_p5
  Multiplexer #(.Bits(5)) multiplexer_11 (
    .sel(signedcomplex_11_p4), .in_0({5{1'b0}}), .in_1(5'b01011), .out(multiplexer_11_out));
  // signedCOMPLEX signedcomplex_13: pin names not known; wires that end beside it: signedcomplex_12_p3, signedcomplex_12_p5, signedcomplex_13_p3, signedcomplex_13_p4, signedcomplex_13_p5
  Multiplexer #(.Bits(5)) multiplexer_12 (
    .sel(signedcomplex_12_p4), .in_0({5{1'b0}}), .in_1(5'b01001), .out(multiplexer_12_out));
  // signedCOMPLEX signedcomplex_14: pin names not known; wires that end beside it: signedcomplex_13_p3, signedcomplex_13_p5, signedcomplex_14_p3, signedcomplex_14_p4, signedcomplex_14_p5
  Multiplexer #(.Bits(5)) multiplexer_13 (
    .sel(signedcomplex_13_p4), .in_0({5{1'b0}}), .in_1(5'b00111), .out(multiplexer_13_out));
  // signedCOMPLEX signedcomplex_15: pin names not known; wires that end beside it: signedcomplex_14_p3, signedcomplex_14_p5, signedcomplex_15_p3, signedcomplex_15_p4, signedcomplex_15_p5
  Multiplexer #(.Bits(5)) multiplexer_14 (
    .sel(signedcomplex_14_p4), .in_0({5{1'b0}}), .in_1(5'b00101), .out(multiplexer_14_out));
  // signedCOMPLEX signedcomplex_16: pin names not known; wires that end beside it: signedcomplex_15_p3, signedcomplex_15_p5, signedcomplex_16_p3
  Multiplexer #(.Bits(5)) multiplexer_15 (
    .sel(signedcomplex_15_p4), .in_0({5{1'b0}}), .in_1(5'b00011), .out(multiplexer_15_out));
  Multiplexer #(.Bits(5)) multiplexer_16 (
    .sel(signedcomplex_16_p3), .in_0({5{1'b0}}), .in_1(5'b00001), .out(multiplexer_16_out));
  Multiplexer #(.Bits(5)) multiplexer_17 (
    .sel(nor_1_out), .in_0({5{1'b0}}), .in_1({5{1'b0}}), .out(multiplexer_17_out));
endmodule
