// Digital circuit test.dig as structural Verilog
module test (
  input  in_1,
  input  [6:0] in_2,
  input  [6:0] in_3,
  input  [4:0] in_4
);

  wire pulldown_2_out;
  wire [14:14] pulldown_1_out;
  wire [15:15] graphiccard_1_d;

  PullDown pulldown_1 (.out(pulldown_1_out[14]));
  GraphicCard #(.graphicHeight(128), .graphicWidth(128), .Bits(16)) graphiccard_1 (
    .A({pulldown_1_out[14], in_3, in_2}), .str(in_1), .C(in_1), .ld(pulldown_2_out), .B(pulldown_2_out),
    .D({graphiccard_1_d[15], in_4, in_4, in_4}));
  PullDown pulldown_2 (.out(pulldown_2_out));
  // also tied to VCC on the sheet: graphiccard_1_d[15]
endmodule
