// Digital circuit mandelplotter.dig as structural Verilog
module mandelplotter (
  input  in_1,
  input  clk,
  input  in_3,
  input  in_4,
  input  [15:0] in_5,
  input  [15:0] in_6
);

  wire comparator_1_eq, comparator_1_gt, comparator_2_eq, comparator_2_gt, comparator_3_eq, comparator_3_gt,
       comparator_4_eq, comparator_4_gt, comparator_5_eq, comparator_5_gt, comparator_6_eq, comparator_6_gt,
       comparator_7_eq, comparator_7_gt, comparator_8_eq, comparator_8_gt, comparator_9_eq, comparator_9_gt,
       comparator_10_eq, comparator_10_gt, comparator_11_eq, comparator_11_gt, comparator_12_eq,
       comparator_12_gt, comparator_13_eq, comparator_13_gt, comparator_14_eq, comparator_14_gt,
       comparator_15_eq, comparator_15_gt, comparator_16_eq, comparator_16_gt, comparator_17_eq,
       comparator_17_gt, comparator_18_eq, comparator_18_gt, comparator_19_eq, comparator_19_gt,
       comparator_20_eq, comparator_20_gt, comparator_21_eq, comparator_21_gt, comparator_22_eq,
       comparator_22_gt, comparator_23_eq, comparator_23_gt, comparator_24_eq, comparator_24_gt,
       comparator_25_eq, comparator_25_gt, comparator_26_eq, comparator_26_gt, comparator_27_eq,
       comparator_27_gt, comparator_28_eq, comparator_28_gt, comparator_29_eq, comparator_29_gt,
       comparator_30_eq, comparator_30_gt, comparator_31_eq, comparator_31_gt, comparator_32_eq,
       comparator_32_gt, graphiccard_1_d, nor_1_out, or_1_out, or_2_out, or_3_out, or_4_out, or_5_out,
       or_6_out, or_7_out, or_8_out, or_9_out, or_10_out, or_11_out, or_12_out, or_13_out, or_14_out,
       or_15_out, or_16_out, or_17_out, or_18_out, or_19_out, or_20_out, or_21_out, or_22_out, or_23_out,
       or_24_out, or_25_out, or_26_out, or_27_out, or_28_out, or_29_out, or_30_out, or_31_out, or_32_out,
       pulldown_2_out, screenmap128_1_screenclock;
  wire [6:0] screenmap128_1_xcoord, screenmap128_1_ycoord;
  wire [14:14] pulldown_1_out;
  wire [15:0] signedcomplex_1_grtrthanfour, signedcomplex_1_newimage, signedcomplex_1_newreals,
       signedcomplex_2_grtrthanfour, signedcomplex_2_newimage, signedcomplex_2_newreals,
       signedcomplex_3_grtrthanfour, signedcomplex_3_newimage, signedcomplex_3_newreals,
       signedcomplex_4_grtrthanfour, signedcomplex_4_newimage, signedcomplex_4_newreals,
       signedcomplex_5_grtrthanfour, signedcomplex_5_newimage, signedcomplex_5_newreals,
       signedcomplex_6_grtrthanfour, signedcomplex_6_newimage, signedcomplex_6_newreals,
       signedcomplex_7_grtrthanfour, signedcomplex_7_newimage, signedcomplex_7_newreals,
       signedcomplex_8_grtrthanfour, signedcomplex_8_newimage, signedcomplex_8_newreals,
       signedcomplex_9_grtrthanfour, signedcomplex_9_newimage, signedcomplex_9_newreals,
       signedcomplex_10_grtrthanfour, signedcomplex_10_newimage, signedcomplex_10_newreals,
       signedcomplex_11_grtrthanfour, signedcomplex_11_newimage, signedcomplex_11_newreals,
       signedcomplex_12_grtrthanfour, signedcomplex_12_newimage, signedcomplex_12_newreals,
       signedcomplex_13_grtrthanfour, signedcomplex_13_newimage, signedcomplex_13_newreals,
       signedcomplex_14_grtrthanfour, signedcomplex_14_newimage, signedcomplex_14_newreals,
       signedcomplex_15_grtrthanfour, signedcomplex_15_newimage, signedcomplex_15_newreals,
       signedcomplex_16_grtrthanfour, signedcomplex_16_newimage, signedcomplex_16_newreals,
       signedcomplex_17_grtrthanfour, signedcomplex_17_newimage, signedcomplex_17_newreals,
       signedcomplex_18_grtrthanfour, signedcomplex_18_newimage, signedcomplex_18_newreals,
       signedcomplex_19_grtrthanfour, signedcomplex_19_newimage, signedcomplex_19_newreals,
       signedcomplex_20_grtrthanfour, signedcomplex_20_newimage, signedcomplex_20_newreals,
       signedcomplex_21_grtrthanfour, signedcomplex_21_newimage, signedcomplex_21_newreals,
       signedcomplex_22_grtrthanfour, signedcomplex_22_newimage, signedcomplex_22_newreals,
       signedcomplex_23_grtrthanfour, signedcomplex_23_newimage, signedcomplex_23_newreals,
       signedcomplex_24_grtrthanfour, signedcomplex_24_newimage, signedcomplex_24_newreals,
       signedcomplex_25_grtrthanfour, signedcomplex_25_newimage, signedcomplex_25_newreals,
       signedcomplex_26_grtrthanfour, signedcomplex_26_newimage, signedcomplex_26_newreals,
       signedcomplex_27_grtrthanfour, signedcomplex_27_newimage, signedcomplex_27_newreals,
       signedcomplex_28_grtrthanfour, signedcomplex_28_newimage, signedcomplex_28_newreals,
       signedcomplex_29_grtrthanfour, signedcomplex_29_newimage, signedcomplex_29_newreals,
       signedcomplex_30_grtrthanfour, signedcomplex_30_newimage, signedcomplex_30_newreals,
       signedcomplex_31_grtrthanfour, signedcomplex_31_newimage, signedcomplex_31_newreals,
       signedcomplex_32_grtrthanfour, signedcomplex_32_newimage, signedcomplex_32_newreals;

  screenMAP128 screenmap128_1 (
    .ResetToNeg2(in_1), .clock(clk), .Xcoord(screenmap128_1_xcoord), .Ycoord(screenmap128_1_ycoord),
    .screenCLOCK(screenmap128_1_screenclock));  // open: mapREAL, mapIMAGE
  PullDown pulldown_1 (.out(pulldown_1_out[14]));
  signedCOMPLEX signedcomplex_1 (
    .A(in_5), .B(in_6), .newIMAGE(signedcomplex_1_newimage), .newREALS(signedcomplex_1_newreals),
    .grtrThanFOUR(signedcomplex_1_grtrthanfour));
  GraphicCard #(.graphicHeight(128), .graphicWidth(128)) graphiccard_1 (
    .A({pulldown_1_out[14], screenmap128_1_ycoord, screenmap128_1_xcoord}), .str(screenmap128_1_screenclock),
    .C(screenmap128_1_screenclock), .ld(pulldown_2_out), .B(pulldown_2_out), .D(graphiccard_1_d));
  PullDown pulldown_2 (.out(pulldown_2_out));
  Comparator #(.Bits(16)) comparator_1 (
    .a(signedcomplex_1_grtrthanfour), .b(16'h4000), .gt(comparator_1_gt), .eq(comparator_1_eq));  // open: lt
  or or_1 (or_1_out, comparator_1_gt, comparator_1_eq);
  Multiplexer multiplexer_1 (.sel(in_3), .in_0(nor_1_out), .in_1(in_4), .out(graphiccard_1_d));
  signedCOMPLEX signedcomplex_2 (
    .A(signedcomplex_1_newimage), .B(signedcomplex_1_newreals), .newIMAGE(signedcomplex_2_newimage),
    .newREALS(signedcomplex_2_newreals), .grtrThanFOUR(signedcomplex_2_grtrthanfour));
  Comparator #(.Bits(16)) comparator_2 (
    .a(signedcomplex_2_grtrthanfour), .b(16'h4000), .gt(comparator_2_gt), .eq(comparator_2_eq));  // open: lt
  or or_2 (or_2_out, comparator_2_gt, comparator_2_eq);
  signedCOMPLEX signedcomplex_3 (
    .A(signedcomplex_2_newimage), .B(signedcomplex_2_newreals), .newIMAGE(signedcomplex_3_newimage),
    .newREALS(signedcomplex_3_newreals), .grtrThanFOUR(signedcomplex_3_grtrthanfour));
  Comparator #(.Bits(16)) comparator_3 (
    .a(signedcomplex_3_grtrthanfour), .b(16'h4000), .gt(comparator_3_gt), .eq(comparator_3_eq));  // open: lt
  signedCOMPLEX signedcomplex_4 (
    .A(signedcomplex_3_newimage), .B(signedcomplex_3_newreals), .newIMAGE(signedcomplex_4_newimage),
    .newREALS(signedcomplex_4_newreals), .grtrThanFOUR(signedcomplex_4_grtrthanfour));
  or or_3 (or_3_out, comparator_3_gt, comparator_3_eq);
  Comparator #(.Bits(16)) comparator_4 (
    .a(signedcomplex_4_grtrthanfour), .b(16'h4000), .gt(comparator_4_gt), .eq(comparator_4_eq));  // open: lt
  signedCOMPLEX signedcomplex_5 (
    .A(signedcomplex_4_newimage), .B(signedcomplex_4_newreals), .newIMAGE(signedcomplex_5_newimage),
    .newREALS(signedcomplex_5_newreals), .grtrThanFOUR(signedcomplex_5_grtrthanfour));
  or or_4 (or_4_out, comparator_4_gt, comparator_4_eq);
  Comparator #(.Bits(16)) comparator_5 (
    .a(signedcomplex_5_grtrthanfour), .b(16'h4000), .gt(comparator_5_gt), .eq(comparator_5_eq));  // open: lt
  or or_5 (or_5_out, comparator_5_gt, comparator_5_eq);
  signedCOMPLEX signedcomplex_6 (
    .A(signedcomplex_5_newimage), .B(signedcomplex_5_newreals), .newIMAGE(signedcomplex_6_newimage),
    .newREALS(signedcomplex_6_newreals), .grtrThanFOUR(signedcomplex_6_grtrthanfour));
  Comparator #(.Bits(16)) comparator_6 (
    .a(signedcomplex_6_grtrthanfour), .b(16'h4000), .gt(comparator_6_gt), .eq(comparator_6_eq));  // open: lt
  or or_6 (or_6_out, comparator_6_gt, comparator_6_eq);
  signedCOMPLEX signedcomplex_7 (
    .A(signedcomplex_6_newimage), .B(signedcomplex_6_newreals), .newIMAGE(signedcomplex_7_newimage),
    .newREALS(signedcomplex_7_newreals), .grtrThanFOUR(signedcomplex_7_grtrthanfour));
  Comparator #(.Bits(16)) comparator_7 (
    .a(signedcomplex_7_grtrthanfour), .b(16'h4000), .gt(comparator_7_gt), .eq(comparator_7_eq));  // open: lt
  signedCOMPLEX signedcomplex_8 (
    .A(signedcomplex_7_newimage), .B(signedcomplex_7_newreals), .newIMAGE(signedcomplex_8_newimage),
    .newREALS(signedcomplex_8_newreals), .grtrThanFOUR(signedcomplex_8_grtrthanfour));
  or or_7 (or_7_out, comparator_7_gt, comparator_7_eq);
  Comparator #(.Bits(16)) comparator_8 (
    .a(signedcomplex_8_grtrthanfour), .b(16'h4000), .gt(comparator_8_gt), .eq(comparator_8_eq));  // open: lt
  signedCOMPLEX signedcomplex_9 (
    .A(signedcomplex_8_newimage), .B(signedcomplex_8_newreals), .newIMAGE(signedcomplex_9_newimage),
    .newREALS(signedcomplex_9_newreals), .grtrThanFOUR(signedcomplex_9_grtrthanfour));
  or or_8 (or_8_out, comparator_8_gt, comparator_8_eq);
  Comparator #(.Bits(16)) comparator_9 (
    .a(signedcomplex_9_grtrthanfour), .b(16'h4000), .gt(comparator_9_gt), .eq(comparator_9_eq));  // open: lt
  or or_9 (or_9_out, comparator_9_gt, comparator_9_eq);
  signedCOMPLEX signedcomplex_10 (
    .A(signedcomplex_9_newimage), .B(signedcomplex_9_newreals), .newIMAGE(signedcomplex_10_newimage),
    .newREALS(signedcomplex_10_newreals), .grtrThanFOUR(signedcomplex_10_grtrthanfour));
  Comparator #(.Bits(16)) comparator_10 (
    .a(signedcomplex_10_grtrthanfour), .b(16'h4000), .gt(comparator_10_gt), .eq(comparator_10_eq));  // open: lt
  or or_10 (or_10_out, comparator_10_gt, comparator_10_eq);
  signedCOMPLEX signedcomplex_11 (
    .A(signedcomplex_10_newimage), .B(signedcomplex_10_newreals), .newIMAGE(signedcomplex_11_newimage),
    .newREALS(signedcomplex_11_newreals), .grtrThanFOUR(signedcomplex_11_grtrthanfour));
  Comparator #(.Bits(16)) comparator_11 (
    .a(signedcomplex_11_grtrthanfour), .b(16'h4000), .gt(comparator_11_gt), .eq(comparator_11_eq));  // open: lt
  signedCOMPLEX signedcomplex_12 (
    .A(signedcomplex_11_newimage), .B(signedcomplex_11_newreals), .newIMAGE(signedcomplex_12_newimage),
    .newREALS(signedcomplex_12_newreals), .grtrThanFOUR(signedcomplex_12_grtrthanfour));
  or or_11 (or_11_out, comparator_11_gt, comparator_11_eq);
  Comparator #(.Bits(16)) comparator_12 (
    .a(signedcomplex_12_grtrthanfour), .b(16'h4000), .gt(comparator_12_gt), .eq(comparator_12_eq));  // open: lt
  signedCOMPLEX signedcomplex_13 (
    .A(signedcomplex_12_newimage), .B(signedcomplex_12_newreals), .newIMAGE(signedcomplex_13_newimage),
    .newREALS(signedcomplex_13_newreals), .grtrThanFOUR(signedcomplex_13_grtrthanfour));
  or or_12 (or_12_out, comparator_12_gt, comparator_12_eq);
  Comparator #(.Bits(16)) comparator_13 (
    .a(signedcomplex_13_grtrthanfour), .b(16'h4000), .gt(comparator_13_gt), .eq(comparator_13_eq));  // open: lt
  or or_13 (or_13_out, comparator_13_gt, comparator_13_eq);
  signedCOMPLEX signedcomplex_14 (
    .A(signedcomplex_13_newimage), .B(signedcomplex_13_newreals), .newIMAGE(signedcomplex_14_newimage),
    .newREALS(signedcomplex_14_newreals), .grtrThanFOUR(signedcomplex_14_grtrthanfour));
  Comparator #(.Bits(16)) comparator_14 (
    .a(signedcomplex_14_grtrthanfour), .b(16'h4000), .gt(comparator_14_gt), .eq(comparator_14_eq));  // open: lt
  or or_14 (or_14_out, comparator_14_gt, comparator_14_eq);
  signedCOMPLEX signedcomplex_15 (
    .A(signedcomplex_14_newimage), .B(signedcomplex_14_newreals), .newIMAGE(signedcomplex_15_newimage),
    .newREALS(signedcomplex_15_newreals), .grtrThanFOUR(signedcomplex_15_grtrthanfour));
  Comparator #(.Bits(16)) comparator_15 (
    .a(signedcomplex_15_grtrthanfour), .b(16'h4000), .gt(comparator_15_gt), .eq(comparator_15_eq));  // open: lt
  signedCOMPLEX signedcomplex_16 (
    .A(signedcomplex_15_newimage), .B(signedcomplex_15_newreals), .newIMAGE(signedcomplex_16_newimage),
    .newREALS(signedcomplex_16_newreals), .grtrThanFOUR(signedcomplex_16_grtrthanfour));
  or or_15 (or_15_out, comparator_15_gt, comparator_15_eq);
  Comparator #(.Bits(16)) comparator_16 (
    .a(signedcomplex_16_grtrthanfour), .b(16'h4000), .gt(comparator_16_gt), .eq(comparator_16_eq));  // open: lt
  signedCOMPLEX signedcomplex_17 (
    .A(signedcomplex_16_newimage), .B(signedcomplex_16_newreals), .newIMAGE(signedcomplex_17_newimage),
    .newREALS(signedcomplex_17_newreals), .grtrThanFOUR(signedcomplex_17_grtrthanfour));
  or or_16 (or_16_out, comparator_16_gt, comparator_16_eq);
  Comparator #(.Bits(16)) comparator_17 (
    .a(signedcomplex_17_grtrthanfour), .b(16'h4000), .gt(comparator_17_gt), .eq(comparator_17_eq));  // open: lt
  or or_17 (or_17_out, comparator_17_gt, comparator_17_eq);
  signedCOMPLEX signedcomplex_18 (
    .A(signedcomplex_17_newimage), .B(signedcomplex_17_newreals), .newIMAGE(signedcomplex_18_newimage),
    .newREALS(signedcomplex_18_newreals), .grtrThanFOUR(signedcomplex_18_grtrthanfour));
  Comparator #(.Bits(16)) comparator_18 (
    .a(signedcomplex_18_grtrthanfour), .b(16'h4000), .gt(comparator_18_gt), .eq(comparator_18_eq));  // open: lt
  or or_18 (or_18_out, comparator_18_gt, comparator_18_eq);
  signedCOMPLEX signedcomplex_19 (
    .A(signedcomplex_18_newimage), .B(signedcomplex_18_newreals), .newIMAGE(signedcomplex_19_newimage),
    .newREALS(signedcomplex_19_newreals), .grtrThanFOUR(signedcomplex_19_grtrthanfour));
  Comparator #(.Bits(16)) comparator_19 (
    .a(signedcomplex_19_grtrthanfour), .b(16'h4000), .gt(comparator_19_gt), .eq(comparator_19_eq));  // open: lt
  signedCOMPLEX signedcomplex_20 (
    .A(signedcomplex_19_newimage), .B(signedcomplex_19_newreals), .newIMAGE(signedcomplex_20_newimage),
    .newREALS(signedcomplex_20_newreals), .grtrThanFOUR(signedcomplex_20_grtrthanfour));
  or or_19 (or_19_out, comparator_19_gt, comparator_19_eq);
  Comparator #(.Bits(16)) comparator_20 (
    .a(signedcomplex_20_grtrthanfour), .b(16'h4000), .gt(comparator_20_gt), .eq(comparator_20_eq));  // open: lt
  signedCOMPLEX signedcomplex_21 (
    .A(signedcomplex_20_newimage), .B(signedcomplex_20_newreals), .newIMAGE(signedcomplex_21_newimage),
    .newREALS(signedcomplex_21_newreals), .grtrThanFOUR(signedcomplex_21_grtrthanfour));
  or or_20 (or_20_out, comparator_20_gt, comparator_20_eq);
  Comparator #(.Bits(16)) comparator_21 (
    .a(signedcomplex_21_grtrthanfour), .b(16'h4000), .gt(comparator_21_gt), .eq(comparator_21_eq));  // open: lt
  or or_21 (or_21_out, comparator_21_gt, comparator_21_eq);
  signedCOMPLEX signedcomplex_22 (
    .A(signedcomplex_21_newimage), .B(signedcomplex_21_newreals), .newIMAGE(signedcomplex_22_newimage),
    .newREALS(signedcomplex_22_newreals), .grtrThanFOUR(signedcomplex_22_grtrthanfour));
  Comparator #(.Bits(16)) comparator_22 (
    .a(signedcomplex_22_grtrthanfour), .b(16'h4000), .gt(comparator_22_gt), .eq(comparator_22_eq));  // open: lt
  or or_22 (or_22_out, comparator_22_gt, comparator_22_eq);
  signedCOMPLEX signedcomplex_23 (
    .A(signedcomplex_22_newimage), .B(signedcomplex_22_newreals), .newIMAGE(signedcomplex_23_newimage),
    .newREALS(signedcomplex_23_newreals), .grtrThanFOUR(signedcomplex_23_grtrthanfour));
  Comparator #(.Bits(16)) comparator_23 (
    .a(signedcomplex_23_grtrthanfour), .b(16'h4000), .gt(comparator_23_gt), .eq(comparator_23_eq));  // open: lt
  signedCOMPLEX signedcomplex_24 (
    .A(signedcomplex_23_newimage), .B(signedcomplex_23_newreals), .newIMAGE(signedcomplex_24_newimage),
    .newREALS(signedcomplex_24_newreals), .grtrThanFOUR(signedcomplex_24_grtrthanfour));
  or or_23 (or_23_out, comparator_23_gt, comparator_23_eq);
  Comparator #(.Bits(16)) comparator_24 (
    .a(signedcomplex_24_grtrthanfour), .b(16'h4000), .gt(comparator_24_gt), .eq(comparator_24_eq));  // open: lt
  signedCOMPLEX signedcomplex_25 (
    .A(signedcomplex_24_newimage), .B(signedcomplex_24_newreals), .newIMAGE(signedcomplex_25_newimage),
    .newREALS(signedcomplex_25_newreals), .grtrThanFOUR(signedcomplex_25_grtrthanfour));
  or or_24 (or_24_out, comparator_24_gt, comparator_24_eq);
  Comparator #(.Bits(16)) comparator_25 (
    .a(signedcomplex_25_grtrthanfour), .b(16'h4000), .gt(comparator_25_gt), .eq(comparator_25_eq));  // open: lt
  or or_25 (or_25_out, comparator_25_gt, comparator_25_eq);
  signedCOMPLEX signedcomplex_26 (
    .A(signedcomplex_25_newimage), .B(signedcomplex_25_newreals), .newIMAGE(signedcomplex_26_newimage),
    .newREALS(signedcomplex_26_newreals), .grtrThanFOUR(signedcomplex_26_grtrthanfour));
  Comparator #(.Bits(16)) comparator_26 (
    .a(signedcomplex_26_grtrthanfour), .b(16'h4000), .gt(comparator_26_gt), .eq(comparator_26_eq));  // open: lt
  or or_26 (or_26_out, comparator_26_gt, comparator_26_eq);
  signedCOMPLEX signedcomplex_27 (
    .A(signedcomplex_26_newimage), .B(signedcomplex_26_newreals), .newIMAGE(signedcomplex_27_newimage),
    .newREALS(signedcomplex_27_newreals), .grtrThanFOUR(signedcomplex_27_grtrthanfour));
  Comparator #(.Bits(16)) comparator_27 (
    .a(signedcomplex_27_grtrthanfour), .b(16'h4000), .gt(comparator_27_gt), .eq(comparator_27_eq));  // open: lt
  signedCOMPLEX signedcomplex_28 (
    .A(signedcomplex_27_newimage), .B(signedcomplex_27_newreals), .newIMAGE(signedcomplex_28_newimage),
    .newREALS(signedcomplex_28_newreals), .grtrThanFOUR(signedcomplex_28_grtrthanfour));
  or or_27 (or_27_out, comparator_27_gt, comparator_27_eq);
  Comparator #(.Bits(16)) comparator_28 (
    .a(signedcomplex_28_grtrthanfour), .b(16'h4000), .gt(comparator_28_gt), .eq(comparator_28_eq));  // open: lt
  signedCOMPLEX signedcomplex_29 (
    .A(signedcomplex_28_newimage), .B(signedcomplex_28_newreals), .newIMAGE(signedcomplex_29_newimage),
    .newREALS(signedcomplex_29_newreals), .grtrThanFOUR(signedcomplex_29_grtrthanfour));
  or or_28 (or_28_out, comparator_28_gt, comparator_28_eq);
  Comparator #(.Bits(16)) comparator_29 (
    .a(signedcomplex_29_grtrthanfour), .b(16'h4000), .gt(comparator_29_gt), .eq(comparator_29_eq));  // open: lt
  or or_29 (or_29_out, comparator_29_gt, comparator_29_eq);
  signedCOMPLEX signedcomplex_30 (
    .A(signedcomplex_29_newimage), .B(signedcomplex_29_newreals), .newIMAGE(signedcomplex_30_newimage),
    .newREALS(signedcomplex_30_newreals), .grtrThanFOUR(signedcomplex_30_grtrthanfour));
  Comparator #(.Bits(16)) comparator_30 (
    .a(signedcomplex_30_grtrthanfour), .b(16'h4000), .gt(comparator_30_gt), .eq(comparator_30_eq));  // open: lt
  or or_30 (or_30_out, comparator_30_gt, comparator_30_eq);
  signedCOMPLEX signedcomplex_31 (
    .A(signedcomplex_30_newimage), .B(signedcomplex_30_newreals), .newIMAGE(signedcomplex_31_newimage),
    .newREALS(signedcomplex_31_newreals), .grtrThanFOUR(signedcomplex_31_grtrthanfour));
  Comparator #(.Bits(16)) comparator_31 (
    .a(signedcomplex_31_grtrthanfour), .b(16'h4000), .gt(comparator_31_gt), .eq(comparator_31_eq));  // open: lt
  signedCOMPLEX signedcomplex_32 (
    .A(signedcomplex_31_newimage), .B(signedcomplex_31_newreals), .newIMAGE(signedcomplex_32_newimage),
    .newREALS(signedcomplex_32_newreals), .grtrThanFOUR(signedcomplex_32_grtrthanfour));
  or or_31 (or_31_out, comparator_31_gt, comparator_31_eq);
  Comparator #(.Bits(16)) comparator_32 (
    .a(signedcomplex_32_grtrthanfour), .b(16'h4000), .gt(comparator_32_gt), .eq(comparator_32_eq));  // open: lt
  or or_32 (or_32_out, comparator_32_gt, comparator_32_eq);
  nor nor_1 (nor_1_out, or_32_out, or_31_out, or_30_out, or_29_out, or_28_out, or_27_out, or_26_out, or_25_out, or_24_out, or_23_out, or_22_out, or_21_out, or_20_out, or_19_out, or_18_out, or_17_out, or_16_out, or_15_out, or_14_out, or_13_out, or_12_out, or_11_out, or_10_out, or_9_out, or_8_out, or_7_out, or_6_out, or_5_out, or_4_out, or_3_out, or_2_out, or_1_out);

  // Notes on the sheet:
  //   clk: Hz: 200
endmodule
