// Digital circuit reals.dig as structural Verilog
module reals (
  input  [15:0] A,
  input  [15:0] B,
  output [15:0] newREALS
);

  wire absunit_1_p2, absunit_2_p2, pulldown_1_out;
  wire [15:0] fixedpointmult_1_p3, fixedpointmult_2_p2, sub_1_s;

  // absunit absunit_1: pin names not known; wires that end beside it: A, absunit_1_p2
  // absunit absunit_2: pin names not known; wires that end beside it: B, absunit_2_p2
  // fixedpointmult fixedpointmult_1: pin names not known; wires that end beside it: absunit_1_p2, A, fixedpointmult_1_p3
  // fixedpointmult fixedpointmult_2: pin names not known; wires that end beside it: absunit_2_p2, fixedpointmult_2_p2
  Sub #(.Bits(16)) sub_1 (
    .a(fixedpointmult_1_p3), .b(fixedpointmult_2_p2), .c_i(pulldown_1_out), .s(sub_1_s));  // open: c_o
  PullDown pulldown_1 (.out(pulldown_1_out));
  Add #(.Bits(16)) add_1 (.a(A), .b(sub_1_s), .c_i(pulldown_1_out), .s(newREALS));  // open: c_o

  // Notes on the sheet:
  //   a
  //   a^2
  //   b^2
  //   real = a^2 - b^2 + a
endmodule
