// Digital circuit screenMAP128.dig as structural Verilog
module screenMAP128 (
  input  ResetToNeg2,
  input  clock,
  output [15:0] mapREAL,
  output [15:0] mapIMAGE,
  output [6:0] Xcoord,
  output [6:0] Ycoord,
  output screenCLOCK
);

  wire and_1_out, and_2_out, and_3_out, and_4_out, and_5_out, and_6_out, and_7_out, comparator_1_eq,
       comparator_2_eq, comparator_3_eq, comparator_4_eq, counter_1_ovf, i_hope_this_works_q,
       multiplexer_1_out, multiplexer_2_out, multiplexer_3_out, or_1_out, or_2_out, or_5_out, or_7_out,
       or_8_out, pulldown_1_out, pulldown_2_out, pulldown_3_out, pulldown_4_out, pulldown_5_out,
       pulldown_6_out;
  wire [7:7] counter_1_out, counter_2_ovf;
  wire [15:0] add_1_s, add_2_s, driver_1_out, driver_2_out, driver_3_out, driver_4_out, or_3_out, or_4_out;

  and and_1 (and_1_out, clock, ~comparator_3_eq);  // And
  assign driver_1_out = or_2_out ? 16'he000 : 16'bz;  // Driver driver_1
  or or_1 (or_1_out, comparator_3_eq, ResetToNeg2);
  assign driver_2_out = or_1_out ? 16'he000 : 16'bz;  // Driver driver_2
  and and_2 (and_2_out, or_1_out, and_1_out);
  and and_3 (and_3_out, clock, ResetToNeg2);
  or or_2 (or_2_out, comparator_2_eq, ResetToNeg2);
  assign or_3_out = driver_3_out | driver_2_out;  // Or or_3, 16 bits wide
  assign or_4_out = driver_4_out | driver_1_out;  // Or or_4, 16 bits wide
  and and_4 (and_4_out, clock, ~comparator_3_eq);  // And
  and and_5 (and_5_out, ResetToNeg2, clock);
  or or_5 (or_5_out, and_2_out, and_3_out, comparator_1_eq);
  and and_6 (and_6_out, ~comparator_2_eq, ~ResetToNeg2);  // And
  Register #(.Bits(16)) register_1 (.D(or_4_out), .C(screenCLOCK), .en(screenCLOCK), .Q(mapREAL));
  or or_6 (screenCLOCK, and_4_out, and_5_out);
  and and_7 (and_7_out, ~comparator_3_eq, ~ResetToNeg2);  // And
  assign driver_3_out = and_7_out ? add_2_s : 16'bz;  // Driver driver_3
  Register #(.Bits(16)) register_2 (.D(or_3_out), .C(or_5_out), .en(or_5_out), .Q(mapIMAGE));
  or or_7 (or_7_out, ResetToNeg2, comparator_1_eq);
  assign driver_4_out = and_6_out ? add_1_s : 16'bz;  // Driver driver_4
  PullDown pulldown_1 (.out(pulldown_1_out));
  Multiplexer multiplexer_1 (.sel(ResetToNeg2), .in_0(screenCLOCK), .in_1(clock), .out(multiplexer_1_out));
  Comparator #(.Bits(16)) comparator_1 (.a(16'he000), .b(mapREAL), .eq(comparator_1_eq));  // open: gt, lt
  Add #(.Bits(16)) add_1 (.a(mapREAL), .b(16'h80), .c_i(pulldown_2_out), .s(add_1_s));  // open: c_o
  PullDown pulldown_2 (.out(pulldown_2_out));
  Add #(.Bits(16)) add_2 (.a(mapIMAGE), .b(16'h80), .c_i(pulldown_3_out), .s(add_2_s));  // open: c_o
  PullDown pulldown_3 (.out(pulldown_3_out));
  Monoflop i_hope_this_works (.C(comparator_1_eq), .R(pulldown_1_out), .Q(i_hope_this_works_q));  // open: nQ
  Counter #(.Bits(8)) counter_1 (
    .en(multiplexer_1_out), .C(multiplexer_1_out), .clr(or_7_out), .out({counter_1_out[7], Xcoord}),
    .ovf(counter_1_ovf));
  Comparator #(.Bits(16)) comparator_2 (.a(16'h2000), .b(mapREAL), .eq(comparator_2_eq));  // open: gt, lt
  Comparator #(.Bits(16)) comparator_3 (.a(16'h2000), .b(mapIMAGE), .eq(comparator_3_eq));  // open: gt, lt
  Multiplexer multiplexer_2 (.sel(ResetToNeg2), .in_0(i_hope_this_works_q), .in_1(clock), .out(multiplexer_2_out));
  PullDown pulldown_4 (.out(pulldown_4_out));
  or or_8 (or_8_out, multiplexer_3_out, ResetToNeg2);
  Seven_Seg_Hex seven_seg_hex_1 (.d(mapREAL[15:12]), .dp(pulldown_5_out));
  Seven_Seg_Hex seven_seg_hex_2 (.d(mapIMAGE[15:12]), .dp(pulldown_6_out));
  Multiplexer multiplexer_3 (
    .sel(comparator_4_eq), .in_0(multiplexer_2_out), .in_1(pulldown_4_out), .out(multiplexer_3_out));
  Seven_Seg_Hex seven_seg_hex_3 (.d(mapREAL[11:8]), .dp(pulldown_5_out));
  Seven_Seg_Hex seven_seg_hex_4 (.d(mapIMAGE[11:8]), .dp(pulldown_6_out));
  Counter #(.Bits(7)) counter_2 (.en(or_8_out), .C(or_8_out), .clr(ResetToNeg2), .out(Ycoord), .ovf(counter_2_ovf[7]));
  Seven_Seg_Hex seven_seg_hex_5 (.d(mapREAL[7:4]), .dp(pulldown_5_out));
  Seven_Seg_Hex seven_seg_hex_6 (.d(mapIMAGE[7:4]), .dp(pulldown_6_out));
  Seven_Seg_Hex seven_seg_hex_7 (.d(mapREAL[3:0]), .dp(pulldown_5_out));
  Seven_Seg_Hex seven_seg_hex_8 (.d(mapIMAGE[3:0]), .dp(pulldown_6_out));
  PullDown pulldown_5 (.out(pulldown_5_out));
  PullDown pulldown_6 (.out(pulldown_6_out));
  Comparator #(.Bits(8)) comparator_4 (
    .a(8'h7f), .b({counter_2_ovf[7], Ycoord}), .eq(comparator_4_eq));  // open: gt, lt
endmodule
