// Digital circuit signedCOMPLEX.dig as structural Verilog
module signedCOMPLEX (
  input  [15:0] A,
  input  [15:0] B,
  output [15:0] newIMAGE,
  output [15:0] newREALS,
  output [15:0] grtrThanFOUR
);

  wire absunit_2_p2, absunit_3_p2, absunit_4_p2, absunit_5_p2, absunit_6_p2, pulldown_1_out, pulldown_2_out,
       pulldown_3_out;
  wire [15:0] absunit_1_p2, add_1_s, arithmetic_shift_out, fixedpointmult_1_p3, fixedpointmult_2_p2,
       fixedpointmult_3_p3, fixedpointmult_4_p3, fixedpointmult_5_p3, multiplexer_1_out, neg_1_out,
       neg_2_out, sub_1_s;

  // absunit absunit_1: pin names not known; wires that end beside it: A, absunit_1_p2
  // absunit absunit_2: pin names not known; wires that end beside it: A, absunit_2_p2
  // absunit absunit_3: pin names not known; wires that end beside it: B, absunit_3_p2
  BarrelShifter #(.barrelShifterMode("arithmetic"), .Bits(16)) arithmetic_shift (
    .in(absunit_1_p2), .shift(5'b00001), .out(arithmetic_shift_out));
  Neg #(.Bits(16)) neg_1 (.in(arithmetic_shift_out), .out(neg_1_out));
  // fixedpointmult fixedpointmult_1: pin names not known; wires that end beside it: absunit_2_p2, A, fixedpointmult_1_p3
  // fixedpointmult fixedpointmult_2: pin names not known; wires that end beside it: absunit_3_p2, fixedpointmult_2_p2
  Multiplexer #(.Bits(16)) multiplexer_1 (
    .sel(A[15]), .in_0(arithmetic_shift_out), .in_1(neg_1_out), .out(multiplexer_1_out));
  PullDown pulldown_1 (.out(pulldown_1_out));
  // absunit absunit_4: pin names not known; wires that end beside it: B, absunit_4_p2
  Sub #(.Bits(16)) sub_1 (
    .a(fixedpointmult_1_p3), .b(fixedpointmult_2_p2), .c_i(pulldown_1_out), .s(sub_1_s));  // open: c_o
  Add #(.Bits(16)) add_1 (.a(16'h1000), .b(multiplexer_1_out), .c_i(pulldown_2_out), .s(add_1_s));  // open: c_o
  PullDown pulldown_2 (.out(pulldown_2_out));
  Add #(.Bits(16)) add_2 (.a(A), .b(sub_1_s), .c_i(pulldown_1_out), .s(newREALS));  // open: c_o
  // fixedpointmult fixedpointmult_3: pin names not known; wires that end beside it: add_1_s, absunit_4_p2, fixedpointmult_3_p3
  // absunit absunit_5: pin names not known; wires that end beside it: newREALS, absunit_5_p2
  // absunit absunit_6: pin names not known; wires that end beside it: newIMAGE, absunit_6_p2
  Neg #(.Bits(16)) neg_2 (.in(fixedpointmult_3_p3), .out(neg_2_out));
  // fixedpointmult fixedpointmult_4: pin names not known; wires that end beside it: absunit_5_p2, absunit_5_p2, fixedpointmult_4_p3
  // fixedpointmult fixedpointmult_5: pin names not known; wires that end beside it: absunit_6_p2, absunit_6_p2, fixedpointmult_5_p3, newIMAGE
  Multiplexer #(.Bits(16)) multiplexer_2 (.sel(B[15]), .in_0(fixedpointmult_3_p3), .in_1(neg_2_out), .out(newIMAGE));
  Add #(.Bits(16)) add_3 (
    .a(fixedpointmult_4_p3), .b(fixedpointmult_5_p3), .c_i(pulldown_3_out), .s(grtrThanFOUR));  // open: c_o
  PullDown pulldown_3 (.out(pulldown_3_out));

  // Notes on the sheet:
  //   a
  //   a^2
  //   b^2
  //   real = a^2 - b^2 + a
endmodule
