// Digital circuit test.dig as structural Verilog
module test (
  input  in_1,
  input  in_2,
  input  [6:0] in_3,
  input  [6:0] in_4
);

  wire pulldown_2_out;
  wire [14:14] pulldown_1_out;

  PullDown pulldown_1 (.out(pulldown_1_out[14]));
  GraphicCard #(.graphicHeight(128), .graphicWidth(128)) graphiccard_1 (
    .A({pulldown_1_out[14], in_4, in_3}), .str(in_2), .C(in_2), .ld(pulldown_2_out), .B(pulldown_2_out),
    .D(in_1));
  PullDown pulldown_2 (.out(pulldown_2_out));
endmodule
